// Logisim project 1 clockCycle button.circ as structural Verilog: 1 circuit, main circuit main
module main (
  input  bi,
  input  Clk,
  output bo
);

  wire and_1_out, and_2_out, not_1_out, not_2_out, not_3_out, not_4_out, not_5_out;
  wire [1:0] and_3_out, register_1_q;

  not not_1 (not_1_out, register_1_q[1]);
  not not_2 (not_2_out, register_1_q[0]);
  not not_3 (not_3_out, register_1_q[1]);
  not not_4 (not_4_out, register_1_q[0]);
  not not_5 (not_5_out, register_1_q[1]);
  and and_1 (and_1_out, not_1_out, register_1_q[0], bi);
  and and_2 (and_2_out, register_1_q[1], not_2_out, bi);
  and and_3 (and_3_out[0], not_3_out, not_4_out, bi);
  and and_4 (bo, not_5_out, register_1_q[0]);
  Register #(.width(2), .Select("low")) register_1 (.D(and_3_out), .Q(register_1_q), .clk(Clk));  // open: en, clr
  or or_1 (and_3_out[1], and_1_out, and_2_out);
endmodule
