// Logisim project Alarme Porta And e flip flop D.circ as structural Verilog: 1 circuit, main circuit main
module main (
  input  in_1,
  input  in_2
);

  wire and_1_out, button_1_out, clock_1_out, counter_1_carry, d_ff_1_q;

  Clock clock_1 (.out(clock_1_out));
  and and_1 (and_1_out, in_1, in_2, counter_1_carry);
  Counter #(.max('h3)) counter_1 (
    .load(in_1), .carry(counter_1_carry), .clk(clock_1_out), .clr(button_1_out));  // open: D, count, Q
  D_Flip_Flop d_ff_1 (.clk(and_1_out), .D(1'b1), .Q(d_ff_1_q), .reset(button_1_out));  // open: Qn, preset, en
  Button button_1 (.out(button_1_out));
  LED led_1 (.in(d_ff_1_q));
endmodule
