// Logisim project Aplicacoes Porta Xnor.circ as structural Verilog: 2 circuits, main circuit main
module main (
  input  in_1,
  input  in_2,
  input  in_3,
  input  in_4,
  input  in_5,
  input  in_6,
  input  in_7,
  input  in_8,
  output out_9,
  output out_10
);

  wire and_1_out, and_2_out, nand_1_out, nor_1_out, not_1_out, not_2_out, not_3_out, not_4_out, not_5_out,
       not_6_out, not_7_out, not_8_out;

  not not_1 (not_1_out, in_1);
  not not_2 (not_2_out, in_2);
  and and_1 (and_1_out, not_1_out, not_2_out, not_3_out, not_4_out);
  not not_3 (not_3_out, in_3);
  not not_4 (not_4_out, in_4);
  nor nor_1 (nor_1_out, in_1, in_2, in_3, in_4);
  not not_5 (not_5_out, in_5);
  not not_6 (not_6_out, in_6);
  and and_2 (and_2_out, not_5_out, not_6_out, not_7_out, not_8_out);
  not not_7 (not_7_out, in_7);
  not not_8 (not_8_out, in_8);
  xnor xnor_1 (out_9, and_1_out, nor_1_out);
  xnor xnor_2 (out_10, and_2_out, nand_1_out);
  nand nand_1 (nand_1_out, in_5, in_6, in_7, in_8);

  // Other names for the same wires on the sheet: A1 = in_1; A2 = in_2; A3 = in_3; A4 = in_4; B1 = in_5; B2 = in_6;
  //   B3 = in_7; B4 = in_8
endmodule

module Xnor (
  input  I1,
  input  I2,
  output O
);

  wire not_1_out, not_2_out;

  not not_1 (not_1_out, I1);
  not not_2 (not_2_out, I2);
  or or_1 (O, not_1_out, not_2_out);
endmodule
