// Logisim project Aplicacoes Porta Xor.circ as structural Verilog: 2 circuits, main circuit main
module main (
  input  in_1,
  input  in_2,
  input  in_3,
  output Resultado_Soma,
  output Carry
);

  wire and_1_out, and_2_out, and_3_out, xor_1_out;

  xor xor_1 (xor_1_out, in_1, in_2);
  and and_1 (and_1_out, in_1, in_2);
  and and_2 (and_2_out, in_2, in_3);
  and and_3 (and_3_out, in_1, in_3);
  xor xor_2 (Resultado_Soma, xor_1_out, in_3);
  or or_1 (Carry, and_1_out, and_2_out, and_3_out);

  // Other names for the same wires on the sheet: A = in_1; B = in_2; C = in_3
endmodule

module carry (
  input  I1,
  input  I2,
  output O
);

  and and_1 (O, I1, I2);
endmodule
