// Logisim project Codificador 4 bits.circ as structural Verilog: 3 circuits, main circuit main
module main (
  input  in_1,
  input  in_2,
  input  in_3,
  input  in_4,
  input  in_5,
  input  in_6,
  input  in_7,
  input  in_8,
  input  in_9,
  output [3:0] out_10
);

  Codificador_4_Bits codificador_4_bits_1 (
    .I1(in_1), .O3(out_10[0]), .I2(in_2), .O2(out_10[1]), .I3(in_3), .I4(in_4), .I5(in_5), .O1(out_10[2]),
    .I6(in_6), .I7(in_7), .O0(out_10[3]), .I8(in_8), .I9(in_9));
endmodule

module Codificador_4_Bits (
  input  I1,
  input  I2,
  input  I3,
  input  I4,
  input  I5,
  input  I6,
  input  I7,
  input  I8,
  input  I9,
  output O3,
  output O2,
  output O1,
  output O0
);

  wire not_1_out, not_2_out, not_3_out, not_4_out, not_5_out, not_6_out, not_7_out, not_8_out, not_9_out,
       not_10_out, not_11_out, not_12_out, not_13_out, not_14_out, not_15_out;

  not not_1 (not_1_out, I8);
  not not_2 (not_2_out, I9);
  not not_3 (not_3_out, I4);
  not not_4 (not_4_out, I5);
  not not_5 (not_5_out, I6);
  not not_6 (not_6_out, I7);
  not not_7 (not_7_out, I2);
  not not_8 (not_8_out, I3);
  not not_9 (not_9_out, I6);
  not not_10 (not_10_out, I7);
  not not_11 (not_11_out, I1);
  not not_12 (not_12_out, I3);
  not not_13 (not_13_out, I5);
  not not_14 (not_14_out, I7);
  not not_15 (not_15_out, I9);
  and and_1 (O3, ~not_1_out, ~not_2_out);  // AND_Gate
  and and_2 (O2, ~not_3_out, ~not_4_out, ~not_5_out, ~not_6_out);  // AND_Gate
  and and_3 (O1, ~not_7_out, ~not_8_out, ~not_9_out, ~not_10_out);  // AND_Gate
  and and_4 (O0, ~not_11_out, ~not_12_out, ~not_13_out, ~not_14_out, ~not_15_out);  // AND_Gate
endmodule

module asd (
  input  I1,
  input  I2,
  input  I3,
  input  I4,
  input  I5,
  input  I6,
  input  I7,
  input  I8,
  input  I9,
  output O3,
  output O2,
  output O1,
  output O0
);

  wire not_1_out, not_2_out, not_3_out, not_4_out, not_5_out, not_6_out, not_7_out, not_8_out, not_9_out,
       not_10_out, not_11_out, not_12_out, not_13_out, not_14_out, not_15_out;

  not not_1 (not_1_out, I8);
  not not_2 (not_2_out, I9);
  not not_3 (not_3_out, I4);
  not not_4 (not_4_out, I5);
  not not_5 (not_5_out, I6);
  not not_6 (not_6_out, I7);
  not not_7 (not_7_out, I2);
  not not_8 (not_8_out, I3);
  not not_9 (not_9_out, I6);
  not not_10 (not_10_out, I7);
  not not_11 (not_11_out, I1);
  not not_12 (not_12_out, I3);
  not not_13 (not_13_out, I5);
  not not_14 (not_14_out, I7);
  not not_15 (not_15_out, I9);
  and and_1 (O3, ~not_1_out, ~not_2_out);  // AND_Gate
  and and_2 (O2, ~not_3_out, ~not_4_out, ~not_5_out, ~not_6_out);  // AND_Gate
  and and_3 (O1, ~not_7_out, ~not_8_out, ~not_9_out, ~not_10_out);  // AND_Gate
  and and_4 (O0, ~not_11_out, ~not_12_out, ~not_13_out, ~not_14_out, ~not_15_out);  // AND_Gate
endmodule
