// Logisim project Codigo de Hamming.circ as structural Verilog: 3 circuits, main circuit main
module main (
  input  [3:0] Entrada,
  input  [6:0] Entrada_2,
  output [6:0] \Saída ,
  output [6:0] \Saída_2 ,
  output [3:0] out_5,
  output [2:0] out_6,
  output [2:0] out_7,
  output [3:0] out_8,
  output [2:0] out_9,
  output [3:0] out_10,
  output [2:0] out_11
);

  wire E1, E2, E3, E4, E5, E6, E7, xor_1_out, xor_2_out, xor_3_out;
  wire [2:0] adder_13_out, multiplier_1_out, multiplier_2_out, multiplier_3_out;
  wire [3:0] adder_1_out, adder_2_out, adder_3_out, adder_7_out, adder_8_out, adder_9_out,
       bit_extender_1_out, bit_extender_2_out, bit_extender_3_out, bit_extender_4_out, bit_extender_5_out,
       bit_extender_6_out, bit_extender_7_out, bit_extender_8_out, bit_extender_9_out, bit_extender_10_out,
       bit_extender_11_out, bit_extender_12_out, bit_extender_13_out, bit_extender_14_out,
       bit_extender_15_out, bit_extender_16_out, bit_extender_17_out, bit_extender_18_out;
  wire [3:1] adder_4_out, adder_5_out, adder_6_out;

  assign bit_extender_1_out = {{3{1'b0}}, Entrada[2]};  // Bit_Extender bit_extender_1
  Adder #(.width(4)) adder_1 (.a(bit_extender_1_out), .b(bit_extender_2_out), .out(adder_1_out));  // open: cin, cout
  assign bit_extender_2_out = {{3{1'b0}}, Entrada[3]};  // Bit_Extender bit_extender_2
  assign bit_extender_3_out = {{3{1'b0}}, Entrada[3]};  // Bit_Extender bit_extender_3
  Adder #(.width(4)) adder_2 (.a(bit_extender_3_out), .b(bit_extender_4_out), .out(adder_2_out));  // open: cin, cout
  assign bit_extender_4_out = {{3{1'b0}}, Entrada[0]};  // Bit_Extender bit_extender_4
  assign bit_extender_5_out = {{3{1'b0}}, Entrada[2]};  // Bit_Extender bit_extender_5
  Adder #(.width(4)) adder_3 (.a(bit_extender_5_out), .b(bit_extender_6_out), .out(adder_3_out));  // open: cin, cout
  assign bit_extender_6_out = {{3{1'b0}}, Entrada[1]};  // Bit_Extender bit_extender_6
  assign bit_extender_7_out = {{3{1'b0}}, Entrada[0]};  // Bit_Extender bit_extender_7
  assign bit_extender_8_out = {{3{1'b0}}, Entrada[1]};  // Bit_Extender bit_extender_8
  assign bit_extender_9_out = {{3{1'b0}}, Entrada[0]};  // Bit_Extender bit_extender_9
  Adder #(.width(4)) adder_4 (
    .a(adder_1_out), .b(bit_extender_7_out), .out({adder_4_out, \Saída [6]}));  // open: cin, cout
  Adder #(.width(4)) adder_5 (
    .a(adder_2_out), .b(bit_extender_8_out), .out({adder_5_out, \Saída [5]}));  // open: cin, cout
  Adder #(.width(4)) adder_6 (
    .a(adder_3_out), .b(bit_extender_9_out), .out({adder_6_out, \Saída [3]}));  // open: cin, cout
  assign bit_extender_10_out = {{3{1'b0}}, Entrada_2[2]};  // Bit_Extender bit_extender_10
  assign bit_extender_11_out = {{3{1'b0}}, Entrada_2[4]};  // Bit_Extender bit_extender_11
  assign bit_extender_12_out = {{3{1'b0}}, Entrada_2[4]};  // Bit_Extender bit_extender_12
  assign bit_extender_13_out = {{3{1'b0}}, Entrada_2[0]};  // Bit_Extender bit_extender_13
  assign bit_extender_14_out = {{3{1'b0}}, Entrada_2[2]};  // Bit_Extender bit_extender_14
  assign bit_extender_15_out = {{3{1'b0}}, Entrada_2[1]};  // Bit_Extender bit_extender_15
  Adder #(.width(4)) adder_7 (.a(bit_extender_10_out), .b(bit_extender_11_out), .out(adder_7_out));  // open: cin, cout
  assign bit_extender_16_out = {{3{1'b0}}, Entrada_2[0]};  // Bit_Extender bit_extender_16
  Adder #(.width(4)) adder_8 (.a(bit_extender_12_out), .b(bit_extender_13_out), .out(adder_8_out));  // open: cin, cout
  assign bit_extender_17_out = {{3{1'b0}}, Entrada_2[1]};  // Bit_Extender bit_extender_17
  Adder #(.width(4)) adder_9 (.a(bit_extender_14_out), .b(bit_extender_15_out), .out(adder_9_out));  // open: cin, cout
  assign bit_extender_18_out = {{3{1'b0}}, Entrada_2[0]};  // Bit_Extender bit_extender_18
  Adder #(.width(4)) adder_10 (.a(adder_7_out), .b(bit_extender_16_out), .out(out_5));  // open: cin, cout
  Adder #(.width(4)) adder_11 (.a(adder_8_out), .b(bit_extender_17_out), .out(out_8));  // open: cin, cout
  Adder #(.width(4)) adder_12 (.a(adder_9_out), .b(bit_extender_18_out), .out(out_10));  // open: cin, cout
  Conserta_Bit_Errado_Hamming conserta_bit_errado_hamming_1 (.Bit(E1), .HammingBit(Entrada_2[6]), .S(\Saída_2 [6]));
  xor xor_1 (xor_1_out, out_5[0], Entrada_2[6]);
  xor xor_2 (xor_2_out, out_8[0], Entrada_2[5]);
  xor xor_3 (xor_3_out, out_10[0], Entrada_2[3]);
  Conserta_Bit_Errado_Hamming conserta_bit_errado_hamming_2 (.Bit(E2), .HammingBit(Entrada_2[5]), .S(\Saída_2 [5]));
  Conserta_Bit_Errado_Hamming conserta_bit_errado_hamming_3 (.Bit(E4), .HammingBit(Entrada_2[3]), .S(\Saída_2 [3]));
  assign out_6 = {{2{1'b0}}, xor_1_out};  // Bit_Extender bit_extender_19
  assign out_9 = {{2{1'b0}}, xor_2_out};  // Bit_Extender bit_extender_20
  assign out_11 = {{2{1'b0}}, xor_3_out};  // Bit_Extender bit_extender_21
  Conserta_Bit_Errado_Hamming conserta_bit_errado_hamming_4 (.Bit(E5), .HammingBit(Entrada_2[2]), .S(\Saída_2 [2]));
  Conserta_Bit_Errado_Hamming conserta_bit_errado_hamming_5 (.Bit(E3), .HammingBit(Entrada_2[4]), .S(\Saída_2 [4]));
  Multiplier #(.width(3)) multiplier_1 (.a(out_6), .b(3'b001), .out(multiplier_1_out));  // open: cin, cout
  Multiplier #(.width(3)) multiplier_2 (.a(out_9), .b(3'b010), .out(multiplier_2_out));  // open: cin, cout
  Multiplier #(.width(3)) multiplier_3 (.a(out_11), .b(3'b100), .out(multiplier_3_out));  // open: cin, cout
  Conserta_Bit_Errado_Hamming conserta_bit_errado_hamming_6 (.Bit(E6), .HammingBit(Entrada_2[1]), .S(\Saída_2 [1]));
  Conserta_Bit_Errado_Hamming conserta_bit_errado_hamming_7 (.Bit(E7), .HammingBit(Entrada_2[0]), .S(\Saída_2 [0]));
  Adder #(.width(3)) adder_13 (.a(multiplier_1_out), .b(multiplier_2_out), .out(adder_13_out));  // open: cin, cout
  Adder #(.width(3)) adder_14 (.a(adder_13_out), .b(multiplier_3_out), .out(out_7));  // open: cin, cout
  Determina_Bit_Errado determina_bit_errado_1 (
    .P1(out_7[2]), .P2(out_7[1]), .P3(out_7[0]), .D1(E1), .D2(E2), .D3(E3), .D4(E4), .D5(E5), .D6(E6), .D7(E7));

  assign {\Saída [4], \Saída [2:0]} = Entrada;

  // Other names for the same wires on the sheet: B0 = Entrada_2[0]; B1 = Entrada_2[1]; B2 = Entrada_2[2];
  //   R3 = Entrada_2[3]; B3 = Entrada_2[4]; R2 = Entrada_2[5]; R1 = Entrada_2[6]; A0 = Entrada[0]; A1 = Entrada[1];
  //   A2 = Entrada[2]; P3 = \Saída [3]; A3 = Entrada[3]; P2 = \Saída [5]; P1 = \Saída [6]

  // Notes on the sheet:
  //   Conserta Bit Errado
  //   Detecta Bit Errado
endmodule

module Determina_Bit_Errado (
  input  P1,
  input  P2,
  input  P3,
  output D1,
  output D2,
  output D3,
  output D4,
  output D5,
  output D6,
  output D7
);

  wire not_1_out, not_2_out, not_3_out, not_4_out, not_5_out, not_6_out, not_7_out, not_8_out, not_9_out;

  not not_1 (not_1_out, P1);
  not not_2 (not_2_out, P2);
  not not_3 (not_3_out, P1);
  not not_4 (not_4_out, P3);
  not not_5 (not_5_out, P1);
  not not_6 (not_6_out, P2);
  not not_7 (not_7_out, P3);
  not not_8 (not_8_out, P2);
  not not_9 (not_9_out, P3);
  and and_1 (D7, P1, P2, P3);
  and and_2 (D1, not_1_out, not_2_out, P3);
  and and_3 (D2, not_3_out, P2, not_4_out);
  and and_4 (D3, not_5_out, P2, P3);
  and and_5 (D4, P1, not_6_out, not_7_out);
  and and_6 (D5, P1, not_8_out, P3);
  and and_7 (D6, P1, P2, not_9_out);
endmodule

module Conserta_Bit_Errado_Hamming (
  input  Bit,
  input  HammingBit,
  output S
);

  wire and_1_out, and_2_out, not_1_out, not_2_out;

  not not_1 (not_1_out, Bit);
  not not_2 (not_2_out, HammingBit);
  and and_1 (and_1_out, not_1_out, HammingBit);
  and and_2 (and_2_out, Bit, not_2_out);
  or or_1 (S, and_1_out, and_2_out);
endmodule
