// Logisim project Comparador 4 Bits.circ as structural Verilog: 3 circuits, main circuit main
module main (
  input  [3:0] in_1,
  input  [3:0] in_2
);

  wire comparador_4_bits_1_a_b, comparador_4_bits_1_a_b_2, comparador_4_bits_1_a_b_3;

  Comparador_4_Bits comparador_4_bits_1 (
    .in_1(in_1), .in_2(in_2), .A_B(comparador_4_bits_1_a_b), .A_B_2(comparador_4_bits_1_a_b_2),
    .A_B_3(comparador_4_bits_1_a_b_3));
  LED led_1 (.in(comparador_4_bits_1_a_b));
  LED led_2 (.in(comparador_4_bits_1_a_b_2));
  LED led_3 (.in(comparador_4_bits_1_a_b_3));
endmodule

module Comparador_1_Bit (
  input  A,
  input  B,
  input  A_B_in,
  input  A_B_in_2,
  input  A_B_in_3,
  output A_B,
  output A_B_2,
  output A_B_3
);

  wire and_1_out, and_2_out, and_3_out, and_5_out, xnor_1_out, xor_1_out;

  xnor xnor_1 (xnor_1_out, A, B);
  xor xor_1 (xor_1_out, A, B);
  and and_1 (and_1_out, A, xor_1_out);
  and and_2 (and_2_out, B, xor_1_out);
  and and_3 (and_3_out, and_1_out, A_B_in_2);
  and and_4 (A_B_2, xnor_1_out, A_B_in_2);
  and and_5 (and_5_out, and_2_out, A_B_in_2);
  or or_1 (A_B, and_3_out, A_B_in);
  or or_2 (A_B_3, and_5_out, A_B_in_3);

  // Other names for the same wires on the sheet: A_B_in_t = A_B_in_3; A_B_in_t_t = A_B_in_2
endmodule

module Comparador_4_Bits (
  input  [3:0] in_1,
  input  [3:0] in_2,
  output A_B,
  output A_B_2,
  output A_B_3
);

  wire comparador_1_bit_1_a_b, comparador_1_bit_1_a_b_2, comparador_1_bit_1_a_b_3, comparador_1_bit_2_a_b,
       comparador_1_bit_2_a_b_2, comparador_1_bit_2_a_b_3, comparador_1_bit_3_a_b, comparador_1_bit_3_a_b_2,
       comparador_1_bit_3_a_b_3;

  Comparador_1_Bit comparador_1_bit_1 (
    .A(in_1[3]), .B(in_2[3]), .A_B_in(1'b0), .A_B_in_2(1'b1), .A_B_in_3(1'b0), .A_B(comparador_1_bit_1_a_b),
    .A_B_2(comparador_1_bit_1_a_b_2), .A_B_3(comparador_1_bit_1_a_b_3));
  Comparador_1_Bit comparador_1_bit_2 (
    .A(in_1[2]), .B(in_2[2]), .A_B_in(comparador_1_bit_1_a_b), .A_B_in_2(comparador_1_bit_1_a_b_2),
    .A_B_in_3(comparador_1_bit_1_a_b_3), .A_B(comparador_1_bit_2_a_b), .A_B_2(comparador_1_bit_2_a_b_2),
    .A_B_3(comparador_1_bit_2_a_b_3));
  Comparador_1_Bit comparador_1_bit_3 (
    .A(in_1[1]), .B(in_2[1]), .A_B_in(comparador_1_bit_2_a_b), .A_B_in_2(comparador_1_bit_2_a_b_2),
    .A_B_in_3(comparador_1_bit_2_a_b_3), .A_B(comparador_1_bit_3_a_b), .A_B_2(comparador_1_bit_3_a_b_2),
    .A_B_3(comparador_1_bit_3_a_b_3));
  Comparador_1_Bit comparador_1_bit_4 (
    .A(in_1[0]), .B(in_2[0]), .A_B_in(comparador_1_bit_3_a_b), .A_B_in_2(comparador_1_bit_3_a_b_2),
    .A_B_in_3(comparador_1_bit_3_a_b_3), .A_B(A_B), .A_B_2(A_B_2), .A_B_3(A_B_3));

  // Other names for the same wires on the sheet: A0 = in_1[0]; A1 = in_1[1]; A2 = in_1[2]; A3 = in_1[3]; B0 = in_2[0];
  //   B1 = in_2[1]; B2 = in_2[2]; B3 = in_2[3]
endmodule
