// Logisim project Contador de frequencia.circ as structural Verilog: 1 circuit, main circuit main
module main (
  input  in_1,
  output [7:0] out_2
);

  wire and_1_out, button_1_out, clock_1_out;

  Clock clock_1 (.out(clock_1_out));
  and and_1 (and_1_out, clock_1_out, in_1);
  Counter counter_1 (.Q(out_2), .clk(and_1_out), .clr(button_1_out));  // open: load, D, count, carry
  Button button_1 (.out(button_1_out));
endmodule
