// Logisim project Decodificador 16 bits.circ as structural Verilog: 7 circuits, main circuit main
module main (
  input  [3:0] in_1,
  input  in_2,
  input  in_3,
  output out_4,
  output out_5,
  output out_6,
  output out_7,
  output out_8,
  output out_9,
  output out_10,
  output out_11,
  output out_12,
  output out_13,
  output out_14,
  output out_15,
  output out_16,
  output out_17,
  output out_18,
  output out_19
);

  asdasd asdasd_1 (
    .Entrada(in_1), .in_2(in_2), .in_3(in_3), .O0(out_4), .O1(out_5), .O2(out_6), .O3(out_7), .O4(out_8),
    .O5(out_9), .O6(out_10), .O7(out_11), .O8(out_12), .O9(out_13), .O10(out_14), .O11(out_15), .O12(out_16),
    .O13(out_17), .O14(out_18), .O15(out_19));
endmodule

module Decod_4x16 (
  input  A3,
  input  A2,
  input  A1,
  input  A0,
  input  in_5,
  input  in_6,
  output O1,
  output O2,
  output O3,
  output O4,
  output O5,
  output O6,
  output O7,
  output O8,
  output O9,
  output O10,
  output O11,
  output O12,
  output O13,
  output O14,
  output O15,
  output O16
);

  wire and_1_out, and_2_out, and_3_out, and_4_out, and_5_out, and_6_out, and_7_out, and_8_out, and_9_out,
       and_10_out, and_11_out, and_12_out, and_13_out, and_14_out, and_15_out, and_16_out, n_CS1_, n_CS2,
       not_3_out, not_4_out, not_5_out, not_6_out, not_7_out, not_8_out, not_9_out, not_10_out, not_11_out,
       not_12_out, not_13_out, not_14_out, not_15_out, not_16_out, not_17_out, not_18_out, not_19_out,
       not_20_out, not_21_out, not_22_out, not_23_out, not_24_out, not_25_out, not_26_out, not_27_out,
       not_28_out, not_29_out, not_30_out, not_31_out, not_32_out, not_33_out, not_34_out;

  not not_1 (n_CS1_, in_5);
  not not_2 (n_CS2, in_6);
  not not_3 (not_3_out, A3);
  not not_4 (not_4_out, A2);
  not not_5 (not_5_out, A1);
  not not_6 (not_6_out, A0);
  not not_7 (not_7_out, A3);
  not not_8 (not_8_out, A2);
  not not_9 (not_9_out, A1);
  not not_10 (not_10_out, A3);
  not not_11 (not_11_out, A2);
  not not_12 (not_12_out, A0);
  not not_13 (not_13_out, A3);
  not not_14 (not_14_out, A2);
  not not_15 (not_15_out, A3);
  not not_16 (not_16_out, A1);
  not not_17 (not_17_out, A0);
  not not_18 (not_18_out, A3);
  not not_19 (not_19_out, A1);
  not not_20 (not_20_out, A3);
  not not_21 (not_21_out, A0);
  not not_22 (not_22_out, A3);
  not not_23 (not_23_out, A2);
  not not_24 (not_24_out, A1);
  not not_25 (not_25_out, A0);
  not not_26 (not_26_out, A2);
  not not_27 (not_27_out, A1);
  not not_28 (not_28_out, A2);
  not not_29 (not_29_out, A0);
  not not_30 (not_30_out, A2);
  not not_31 (not_31_out, A1);
  not not_32 (not_32_out, A0);
  not not_33 (not_33_out, A1);
  not not_34 (not_34_out, A0);
  and and_1 (and_1_out, A3, A2, A1, A0);
  and and_2 (and_2_out, not_3_out, not_4_out, not_5_out, not_6_out);
  and and_3 (and_3_out, not_7_out, not_8_out, not_9_out, A0);
  and and_4 (and_4_out, not_10_out, not_11_out, A1, not_12_out);
  and and_5 (and_5_out, not_13_out, not_14_out, A1, A0);
  and and_6 (and_6_out, not_15_out, A2, not_16_out, not_17_out);
  and and_7 (and_7_out, not_18_out, A2, not_19_out, A0);
  and and_8 (and_8_out, not_20_out, A2, A1, not_21_out);
  and and_9 (and_9_out, not_22_out, A2, A1, A0);
  and and_10 (and_10_out, A3, not_23_out, not_24_out, not_25_out);
  and and_11 (and_11_out, A3, not_26_out, not_27_out, A0);
  and and_12 (and_12_out, A3, not_28_out, A1, not_29_out);
  and and_13 (and_13_out, A3, not_30_out, A1, A0);
  and and_14 (and_14_out, A3, A2, not_31_out, not_32_out);
  and and_15 (and_15_out, A3, A2, not_33_out, A0);
  and and_16 (and_16_out, A3, A2, A1, not_34_out);
  and and_17 (O1, and_2_out, n_CS1_, n_CS2);
  and and_18 (O2, and_3_out, n_CS1_, n_CS2);
  and and_19 (O3, and_4_out, n_CS1_, n_CS2);
  and and_20 (O4, and_5_out, n_CS1_, n_CS2);
  and and_21 (O5, and_6_out, n_CS1_, n_CS2);
  and and_22 (O6, and_7_out, n_CS1_, n_CS2);
  and and_23 (O7, and_8_out, n_CS1_, n_CS2);
  and and_24 (O8, and_9_out, n_CS1_, n_CS2);
  and and_25 (O9, and_10_out, n_CS1_, n_CS2);
  and and_26 (O10, and_11_out, n_CS1_, n_CS2);
  and and_27 (O11, and_12_out, n_CS1_, n_CS2);
  and and_28 (O12, and_13_out, n_CS1_, n_CS2);
  and and_29 (O13, and_14_out, n_CS1_, n_CS2);
  and and_30 (O14, and_15_out, n_CS1_, n_CS2);
  and and_31 (O15, and_16_out, n_CS1_, n_CS2);
  and and_32 (O16, and_1_out, n_CS1_, n_CS2);
endmodule

module asd (
  input  A3,
  input  in_2,
  input  A2,
  input  in_4,
  input  A1,
  input  A0,
  output O0,
  output O1,
  output O2,
  output O3,
  output O4,
  output O5,
  output O6,
  output O7,
  output O8,
  output O9,
  output O10,
  output O11,
  output O12,
  output O13,
  output O14,
  output O15,
  output O16
);

  wire B0, B1, B2, B3, B4, B5, B6, B7, B8, B9, B10, B11, B12, B13, B14, B15, n_CS1_, n_CS2, not_1_out,
       not_2_out, not_3_out, not_4_out, not_5_out, not_6_out, not_7_out, not_8_out, not_9_out, not_10_out,
       not_11_out, not_12_out, not_13_out, not_14_out, not_15_out, not_16_out, not_17_out, not_18_out,
       not_19_out, not_20_out, not_21_out, not_22_out, not_23_out, not_24_out, not_25_out, not_26_out,
       not_27_out, not_28_out, not_29_out, not_30_out, not_31_out, not_32_out, not_33_out, not_34_out,
       not_35_out, not_36_out, not_37_out, not_38_out, not_39_out, not_40_out, not_41_out, not_42_out,
       not_43_out, not_44_out, not_45_out, not_46_out, not_47_out, not_48_out, not_49_out;

  not not_1 (not_1_out, A3);
  not not_2 (not_2_out, A2);
  not not_3 (not_3_out, A1);
  not not_4 (not_4_out, A0);
  not not_5 (not_5_out, A3);
  not not_6 (not_6_out, A2);
  not not_7 (not_7_out, A1);
  not not_8 (not_8_out, A3);
  not not_9 (not_9_out, A2);
  not not_10 (not_10_out, A0);
  not not_11 (not_11_out, A3);
  not not_12 (not_12_out, A2);
  not not_13 (not_13_out, A3);
  not not_14 (not_14_out, A1);
  not not_15 (not_15_out, A0);
  not not_16 (not_16_out, A3);
  not not_17 (not_17_out, A1);
  not not_18 (not_18_out, A3);
  not not_19 (not_19_out, A0);
  not not_20 (not_20_out, A3);
  not not_21 (not_21_out, A2);
  not not_22 (not_22_out, A1);
  not not_23 (not_23_out, A0);
  not not_24 (not_24_out, A2);
  not not_25 (not_25_out, A1);
  not not_26 (not_26_out, A2);
  not not_27 (not_27_out, A0);
  not not_28 (not_28_out, A2);
  not not_29 (not_29_out, A1);
  not not_30 (not_30_out, A0);
  not not_31 (not_31_out, A1);
  not not_32 (not_32_out, A0);
  and and_1 (B15, A3, A2, A1, A0);
  and and_2 (B0, not_1_out, not_2_out, not_3_out, not_4_out);
  and and_3 (B1, not_5_out, not_6_out, not_7_out, A0);
  and and_4 (B2, not_8_out, not_9_out, A1, not_10_out);
  and and_5 (B3, not_11_out, not_12_out, A1, A0);
  and and_6 (B4, not_13_out, A2, not_14_out, not_15_out);
  and and_7 (B5, not_16_out, A2, not_17_out, A0);
  and and_8 (B6, not_18_out, A2, A1, not_19_out);
  and and_9 (B7, not_20_out, A2, A1, A0);
  and and_10 (B8, A3, not_21_out, not_22_out, not_23_out);
  and and_11 (B9, A3, not_24_out, not_25_out, A0);
  and and_12 (B10, A3, not_26_out, A1, not_27_out);
  and and_13 (B11, A3, not_28_out, A1, A0);
  and and_14 (B12, A3, A2, not_29_out, not_30_out);
  and and_15 (B13, A3, A2, not_31_out, A0);
  and and_16 (B14, A3, A2, A1, not_32_out);
  not not_33 (not_33_out, B0);
  not not_34 (not_34_out, B1);
  not not_35 (not_35_out, B2);
  not not_36 (not_36_out, B3);
  not not_37 (not_37_out, B4);
  not not_38 (not_38_out, B5);
  not not_39 (not_39_out, B6);
  not not_40 (not_40_out, B7);
  not not_41 (not_41_out, B8);
  not not_42 (not_42_out, B9);
  not not_43 (not_43_out, B10);
  not not_44 (not_44_out, B11);
  not not_45 (not_45_out, B12);
  not not_46 (not_46_out, B13);
  not not_47 (not_47_out, B14);
  not not_48 (not_48_out, B15);
  not not_49 (not_49_out, 1'b0);
  Multiplexador_4bits multiplexador_4bits_1 (
    .in_1(n_CS2), .in_2(n_CS1_), .in_3(not_33_out), .in_4(B0), .in_5(B0), .in_6(B0), .out_7(O0));
  Multiplexador_4bits multiplexador_4bits_2 (
    .in_1(n_CS2), .in_2(n_CS1_), .in_3(not_34_out), .in_4(B1), .in_5(B1), .in_6(B1), .out_7(O1));
  Multiplexador_4bits multiplexador_4bits_3 (
    .in_1(n_CS2), .in_2(n_CS1_), .in_3(not_35_out), .in_4(B2), .in_5(B2), .in_6(B2), .out_7(O2));
  Multiplexador_4bits multiplexador_4bits_4 (
    .in_1(n_CS2), .in_2(n_CS1_), .in_3(not_36_out), .in_4(B3), .in_5(B3), .in_6(B3), .out_7(O3));
  Multiplexador_4bits multiplexador_4bits_5 (
    .in_1(n_CS2), .in_2(n_CS1_), .in_3(not_37_out), .in_4(B4), .in_5(B4), .in_6(B4), .out_7(O4));
  Multiplexador_4bits multiplexador_4bits_6 (
    .in_1(n_CS2), .in_2(n_CS1_), .in_3(not_38_out), .in_4(B5), .in_5(B5), .in_6(B5), .out_7(O5));
  Multiplexador_4bits multiplexador_4bits_7 (
    .in_1(n_CS2), .in_2(n_CS1_), .in_3(not_39_out), .in_4(B6), .in_5(B6), .in_6(B6), .out_7(O6));
  Multiplexador_4bits multiplexador_4bits_8 (
    .in_1(n_CS2), .in_2(n_CS1_), .in_3(not_40_out), .in_4(B7), .in_5(B7), .in_6(B7), .out_7(O7));
  Multiplexador_4bits multiplexador_4bits_9 (
    .in_1(n_CS2), .in_2(n_CS1_), .in_3(not_41_out), .in_4(B8), .in_5(B8), .in_6(B8), .out_7(O8));
  Multiplexador_4bits multiplexador_4bits_10 (
    .in_1(n_CS2), .in_2(n_CS1_), .in_3(not_42_out), .in_4(B9), .in_5(B9), .in_6(B9), .out_7(O9));
  Multiplexador_4bits multiplexador_4bits_11 (
    .in_1(n_CS2), .in_2(n_CS1_), .in_3(not_43_out), .in_4(B10), .in_5(B10), .in_6(B10), .out_7(O10));
  Multiplexador_4bits multiplexador_4bits_12 (
    .in_1(n_CS2), .in_2(n_CS1_), .in_3(not_44_out), .in_4(B11), .in_5(B11), .in_6(B11), .out_7(O11));
  Multiplexador_4bits multiplexador_4bits_13 (
    .in_1(n_CS2), .in_2(n_CS1_), .in_3(not_45_out), .in_4(B12), .in_5(B12), .in_6(B12), .out_7(O12));
  Multiplexador_4bits multiplexador_4bits_14 (
    .in_1(n_CS2), .in_2(n_CS1_), .in_3(not_46_out), .in_4(B13), .in_5(B13), .in_6(B13), .out_7(O13));
  Multiplexador_4bits multiplexador_4bits_15 (
    .in_1(n_CS2), .in_2(n_CS1_), .in_3(not_47_out), .in_4(B14), .in_5(B14), .in_6(B14), .out_7(O14));
  Multiplexador_4bits multiplexador_4bits_16 (
    .in_1(n_CS2), .in_2(n_CS1_), .in_3(not_48_out), .in_4(B15), .in_5(B15), .in_6(B15), .out_7(O15));
  Multiplexador_4bits multiplexador_4bits_17 (
    .in_1(n_CS2), .in_2(n_CS1_), .in_3(not_49_out), .in_4(1'b0), .in_5(1'b0), .in_6(1'b0), .out_7(O16));
  not not_50 (n_CS1_, in_2);
  not not_51 (n_CS2, in_4);
endmodule

module Multiplexador_4bits (
  input  in_1,
  input  in_2,
  input  in_3,
  input  in_4,
  input  in_5,
  input  in_6,
  output out_7
);

  wire and_1_out, and_2_out, and_3_out, and_4_out;

  and and_1 (and_1_out, in_3, ~in_2, ~in_1);  // AND_Gate
  and and_2 (and_2_out, in_4, ~in_2, in_1);  // AND_Gate
  and and_3 (and_3_out, in_5, in_2, ~in_1);  // AND_Gate
  and and_4 (and_4_out, in_6, in_2, in_1);
  or or_1 (out_7, and_1_out, and_2_out, and_3_out, and_4_out);

  // Other names for the same wires on the sheet: D0 = in_3; D1 = in_4; D2 = in_5; D3 = in_6; S0 = in_1; S1 = in_2
endmodule

module asdasd (
  input  [3:0] Entrada,
  input  in_2,
  input  in_3,
  output O0,
  output O1,
  output O2,
  output O3,
  output O4,
  output O5,
  output O6,
  output O7,
  output O8,
  output O9,
  output O10,
  output O11,
  output O12,
  output O13,
  output O14,
  output O15
);

  wire B0, B1, B2, B3, B4, B5, B6, B7, B8, B9, B10, B11, B12, B13, B14, B15, n_CS1_, n_CS2, not_1_out,
       not_2_out, not_3_out, not_4_out, not_5_out, not_6_out, not_7_out, not_8_out, not_9_out, not_10_out,
       not_11_out, not_12_out, not_13_out, not_14_out, not_15_out, not_16_out, not_17_out, not_18_out,
       not_19_out, not_20_out, not_21_out, not_22_out, not_23_out, not_24_out, not_25_out, not_26_out,
       not_27_out, not_28_out, not_29_out, not_30_out, not_31_out, not_32_out, not_33_out, not_34_out,
       not_35_out, not_36_out, not_37_out, not_38_out, not_39_out, not_40_out, not_41_out, not_42_out,
       not_43_out, not_44_out, not_45_out, not_46_out, not_47_out, not_48_out;

  not not_1 (not_1_out, Entrada[3]);
  not not_2 (not_2_out, Entrada[2]);
  not not_3 (not_3_out, Entrada[1]);
  not not_4 (not_4_out, Entrada[0]);
  not not_5 (not_5_out, Entrada[3]);
  not not_6 (not_6_out, Entrada[2]);
  not not_7 (not_7_out, Entrada[1]);
  not not_8 (not_8_out, Entrada[3]);
  not not_9 (not_9_out, Entrada[2]);
  not not_10 (not_10_out, Entrada[0]);
  not not_11 (not_11_out, Entrada[3]);
  not not_12 (not_12_out, Entrada[2]);
  not not_13 (not_13_out, Entrada[3]);
  not not_14 (not_14_out, Entrada[1]);
  not not_15 (not_15_out, Entrada[0]);
  not not_16 (not_16_out, Entrada[3]);
  not not_17 (not_17_out, Entrada[1]);
  not not_18 (not_18_out, Entrada[3]);
  not not_19 (not_19_out, Entrada[0]);
  not not_20 (not_20_out, Entrada[3]);
  not not_21 (not_21_out, Entrada[2]);
  not not_22 (not_22_out, Entrada[1]);
  not not_23 (not_23_out, Entrada[0]);
  not not_24 (not_24_out, Entrada[2]);
  not not_25 (not_25_out, Entrada[1]);
  not not_26 (not_26_out, Entrada[2]);
  not not_27 (not_27_out, Entrada[0]);
  not not_28 (not_28_out, Entrada[2]);
  not not_29 (not_29_out, Entrada[1]);
  not not_30 (not_30_out, Entrada[0]);
  not not_31 (not_31_out, Entrada[1]);
  not not_32 (not_32_out, Entrada[0]);
  and and_1 (B15, Entrada[3], Entrada[2], Entrada[1], Entrada[0]);
  and and_2 (B0, not_1_out, not_2_out, not_3_out, not_4_out);
  and and_3 (B1, not_5_out, not_6_out, not_7_out, Entrada[0]);
  and and_4 (B2, not_8_out, not_9_out, Entrada[1], not_10_out);
  and and_5 (B3, not_11_out, not_12_out, Entrada[1], Entrada[0]);
  and and_6 (B4, not_13_out, Entrada[2], not_14_out, not_15_out);
  and and_7 (B5, not_16_out, Entrada[2], not_17_out, Entrada[0]);
  and and_8 (B6, not_18_out, Entrada[2], Entrada[1], not_19_out);
  and and_9 (B7, not_20_out, Entrada[2], Entrada[1], Entrada[0]);
  and and_10 (B8, Entrada[3], not_21_out, not_22_out, not_23_out);
  and and_11 (B9, Entrada[3], not_24_out, not_25_out, Entrada[0]);
  and and_12 (B10, Entrada[3], not_26_out, Entrada[1], not_27_out);
  and and_13 (B11, Entrada[3], not_28_out, Entrada[1], Entrada[0]);
  and and_14 (B12, Entrada[3], Entrada[2], not_29_out, not_30_out);
  and and_15 (B13, Entrada[3], Entrada[2], not_31_out, Entrada[0]);
  and and_16 (B14, Entrada[3], Entrada[2], Entrada[1], not_32_out);
  not not_33 (not_33_out, B0);
  not not_34 (not_34_out, B1);
  not not_35 (not_35_out, B2);
  not not_36 (not_36_out, B3);
  not not_37 (not_37_out, B4);
  not not_38 (not_38_out, B5);
  not not_39 (not_39_out, B6);
  not not_40 (not_40_out, B7);
  not not_41 (not_41_out, B8);
  not not_42 (not_42_out, B9);
  not not_43 (not_43_out, B10);
  not not_44 (not_44_out, B11);
  not not_45 (not_45_out, B12);
  not not_46 (not_46_out, B13);
  not not_47 (not_47_out, B14);
  not not_48 (not_48_out, B15);
  Multiplexador_4bits multiplexador_4bits_1 (
    .in_1(n_CS2), .in_2(n_CS1_), .in_3(not_33_out), .in_4(B0), .in_5(B0), .in_6(B0), .out_7(O0));
  Multiplexador_4bits multiplexador_4bits_2 (
    .in_1(n_CS2), .in_2(n_CS1_), .in_3(not_34_out), .in_4(B1), .in_5(B1), .in_6(B1), .out_7(O1));
  Multiplexador_4bits multiplexador_4bits_3 (
    .in_1(n_CS2), .in_2(n_CS1_), .in_3(not_35_out), .in_4(B2), .in_5(B2), .in_6(B2), .out_7(O2));
  Multiplexador_4bits multiplexador_4bits_4 (
    .in_1(n_CS2), .in_2(n_CS1_), .in_3(not_36_out), .in_4(B3), .in_5(B3), .in_6(B3), .out_7(O3));
  Multiplexador_4bits multiplexador_4bits_5 (
    .in_1(n_CS2), .in_2(n_CS1_), .in_3(not_37_out), .in_4(B4), .in_5(B4), .in_6(B4), .out_7(O4));
  Multiplexador_4bits multiplexador_4bits_6 (
    .in_1(n_CS2), .in_2(n_CS1_), .in_3(not_38_out), .in_4(B5), .in_5(B5), .in_6(B5), .out_7(O5));
  Multiplexador_4bits multiplexador_4bits_7 (
    .in_1(n_CS2), .in_2(n_CS1_), .in_3(not_39_out), .in_4(B6), .in_5(B6), .in_6(B6), .out_7(O6));
  Multiplexador_4bits multiplexador_4bits_8 (
    .in_1(n_CS2), .in_2(n_CS1_), .in_3(not_40_out), .in_4(B7), .in_5(B7), .in_6(B7), .out_7(O7));
  Multiplexador_4bits multiplexador_4bits_9 (
    .in_1(n_CS2), .in_2(n_CS1_), .in_3(not_41_out), .in_4(B8), .in_5(B8), .in_6(B8), .out_7(O8));
  Multiplexador_4bits multiplexador_4bits_10 (
    .in_1(n_CS2), .in_2(n_CS1_), .in_3(not_42_out), .in_4(B9), .in_5(B9), .in_6(B9), .out_7(O9));
  Multiplexador_4bits multiplexador_4bits_11 (
    .in_1(n_CS2), .in_2(n_CS1_), .in_3(not_43_out), .in_4(B10), .in_5(B10), .in_6(B10), .out_7(O10));
  Multiplexador_4bits multiplexador_4bits_12 (
    .in_1(n_CS2), .in_2(n_CS1_), .in_3(not_44_out), .in_4(B11), .in_5(B11), .in_6(B11), .out_7(O11));
  Multiplexador_4bits multiplexador_4bits_13 (
    .in_1(n_CS2), .in_2(n_CS1_), .in_3(not_45_out), .in_4(B12), .in_5(B12), .in_6(B12), .out_7(O12));
  Multiplexador_4bits multiplexador_4bits_14 (
    .in_1(n_CS2), .in_2(n_CS1_), .in_3(not_46_out), .in_4(B13), .in_5(B13), .in_6(B13), .out_7(O13));
  Multiplexador_4bits multiplexador_4bits_15 (
    .in_1(n_CS2), .in_2(n_CS1_), .in_3(not_47_out), .in_4(B14), .in_5(B14), .in_6(B14), .out_7(O14));
  Multiplexador_4bits multiplexador_4bits_16 (
    .in_1(n_CS2), .in_2(n_CS1_), .in_3(not_48_out), .in_4(B15), .in_5(B15), .in_6(B15), .out_7(O15));
  not not_49 (n_CS1_, in_2);
  not not_50 (n_CS2, in_3);
endmodule

module Codificador_4_bits_nivel_baixo (
  input  I1,
  input  I2,
  input  I3,
  input  I4,
  input  I5,
  input  I6,
  input  I7,
  input  I8,
  input  I9,
  output O3,
  output O2,
  output O1,
  output O0
);

  wire not_1_out, not_2_out, not_3_out, not_4_out, not_5_out, not_6_out, not_7_out, not_8_out, not_9_out,
       not_10_out, not_11_out, not_12_out, not_13_out, not_14_out, not_15_out;

  not not_1 (not_1_out, I8);
  not not_2 (not_2_out, I9);
  not not_3 (not_3_out, I4);
  not not_4 (not_4_out, I5);
  not not_5 (not_5_out, I6);
  not not_6 (not_6_out, I7);
  not not_7 (not_7_out, I2);
  not not_8 (not_8_out, I3);
  not not_9 (not_9_out, I6);
  not not_10 (not_10_out, I7);
  not not_11 (not_11_out, I1);
  not not_12 (not_12_out, I3);
  not not_13 (not_13_out, I5);
  not not_14 (not_14_out, I7);
  not not_15 (not_15_out, I9);
  and and_1 (O3, ~not_1_out, ~not_2_out);  // AND_Gate
  and and_2 (O2, ~not_3_out, ~not_4_out, ~not_5_out, ~not_6_out);  // AND_Gate
  and and_3 (O1, ~not_7_out, ~not_8_out, ~not_9_out, ~not_10_out);  // AND_Gate
  and and_4 (O0, ~not_11_out, ~not_12_out, ~not_13_out, ~not_14_out, ~not_15_out);  // AND_Gate
endmodule

module Mux_8_Bits (
  input  in_1,
  input  in_2,
  input  in_3,
  input  in_4,
  input  in_5,
  input  in_6,
  input  in_7,
  input  in_8,
  input  in_9,
  input  in_10,
  input  in_11,
  output out_12
);

  wire and_1_out, and_2_out, codificador_4_bits_nivel_baixo_1_o0, codificador_4_bits_nivel_baixo_1_o1,
       codificador_4_bits_nivel_baixo_1_o2, codificador_4_bits_nivel_baixo_1_o3,
       codificador_4_bits_nivel_baixo_2_o0, codificador_4_bits_nivel_baixo_2_o1,
       codificador_4_bits_nivel_baixo_2_o2, codificador_4_bits_nivel_baixo_2_o3, multiplexador_4bits_1_out_7,
       multiplexador_4bits_2_out_7, not_1_out, not_2_out, not_3_out, not_4_out, not_5_out, not_6_out,
       not_7_out, not_10_out, not_11_out, not_14_out, not_15_out, or_1_out, or_2_out;

  not not_1 (not_1_out, in_1);
  not not_2 (not_2_out, in_2);
  not not_3 (not_3_out, in_3);
  not not_4 (not_4_out, in_5);
  not not_5 (not_5_out, in_6);
  not not_6 (not_6_out, in_7);
  or or_1 (or_1_out, not_1_out, not_2_out, not_3_out);
  and and_1 (and_1_out, ~not_1_out, ~not_2_out, ~not_3_out);  // AND_Gate
  and and_2 (and_2_out, ~not_4_out, ~not_5_out, ~not_5_out);  // AND_Gate
  or or_2 (or_2_out, and_1_out, or_1_out);
  not not_7 (not_7_out, or_2_out);
  // OR_Gate or_3 has open pins: in0=and_2_out, in1=not_6_out, out=open
  Codificador_4_bits_nivel_baixo codificador_4_bits_nivel_baixo_1 (
    .I1(not_1_out), .I2(not_2_out), .I3(not_3_out), .I4(1'b1), .I5(1'b1), .I6(1'b1), .I7(1'b1), .I8(1'b1),
    .I9(1'b1), .O3(codificador_4_bits_nivel_baixo_1_o3), .O2(codificador_4_bits_nivel_baixo_1_o2),
    .O1(codificador_4_bits_nivel_baixo_1_o1), .O0(codificador_4_bits_nivel_baixo_1_o0));
  // NOT_Gate not_8 has open pins: in=codificador_4_bits_nivel_baixo_1_o3, out=open
  // NOT_Gate not_9 has open pins: in=codificador_4_bits_nivel_baixo_1_o2, out=open
  not not_10 (not_10_out, codificador_4_bits_nivel_baixo_1_o1);
  not not_11 (not_11_out, codificador_4_bits_nivel_baixo_1_o0);
  // NOT_Gate not_12 has open pins: in=codificador_4_bits_nivel_baixo_2_o3, out=open
  Codificador_4_bits_nivel_baixo codificador_4_bits_nivel_baixo_2 (
    .I1(not_4_out), .I2(not_5_out), .I3(not_6_out), .I4(1'b1), .I5(1'b1), .I6(1'b1), .I7(1'b1), .I8(1'b1),
    .I9(1'b1), .O3(codificador_4_bits_nivel_baixo_2_o3), .O2(codificador_4_bits_nivel_baixo_2_o2),
    .O1(codificador_4_bits_nivel_baixo_2_o1), .O0(codificador_4_bits_nivel_baixo_2_o0));
  // NOT_Gate not_13 has open pins: in=codificador_4_bits_nivel_baixo_2_o2, out=open
  not not_14 (not_14_out, codificador_4_bits_nivel_baixo_2_o1);
  not not_15 (not_15_out, codificador_4_bits_nivel_baixo_2_o0);
  Multiplexador_4bits multiplexador_4bits_1 (
    .in_1(not_15_out), .in_2(not_14_out), .in_3(in_8), .in_4(in_9), .in_5(in_10), .in_6(in_11),
    .out_7(multiplexador_4bits_1_out_7));
  Multiplexador_4bits multiplexador_4bits_2 (
    .in_1(not_11_out), .in_2(not_10_out), .in_3(in_4), .out_7(multiplexador_4bits_2_out_7));  // open: in_4, in_5, in_6
  Multiplexador_4bits multiplexador_4bits_3 (
    .in_1(not_7_out), .in_2(1'b0), .in_3(multiplexador_4bits_2_out_7), .in_4(multiplexador_4bits_1_out_7),
    .out_7(out_12));  // open: in_5, in_6
endmodule
