// Logisim project Divisor de frequencia.circ as structural Verilog: 1 circuit, main circuit main
module main (
);

  wire CLK, Qa, Qb, Saida;

  Clock clock_1 (.out(CLK));
  // Digital_Oscilloscope digital_oscilloscope_1: pin names not known; wires that end beside it: CLK, Qa, Qb, Saida
  J_K_Flip_Flop #(.Pre_Clr_Positions("LEGACY"), .enable("true")) j_k_ff_1 (
    .J(1'b1), .clk(CLK), .K(1'b1), .Q(Qa));  // open: Qn, preset, en, reset
  J_K_Flip_Flop j_k_ff_2 (.J(1'b1), .clk(Qa), .K(1'b1), .Q(Qb));  // open: Qn, preset, reset
  J_K_Flip_Flop j_k_ff_3 (.J(1'b1), .clk(Qb), .K(1'b1), .Q(Saida));  // open: Qn, preset, reset
endmodule
