// Logisim project Event Detector flip flop D.circ as structural Verilog: 1 circuit, main circuit main
module main (
);

  wire button_1_out, button_2_out, d_ff_1_q;

  Button button_1 (.out(button_1_out));
  D_Flip_Flop d_ff_1 (.clk(button_1_out), .D(1'b1), .Q(d_ff_1_q), .reset(button_2_out));  // open: Qn, preset, en
  Button button_2 (.out(button_2_out));
  LED led_1 (.in(d_ff_1_q));
endmodule
