// Logisim project FlipFlopD.circ as structural Verilog: 3 circuits, main circuit main
module main (
  input  Data,
  input  D,
  input  EN,
  input  J,
  input  S,
  input  K,
  input  EN_2,
  input  R,
  input  K_2,
  input  J_2,
  output out_11,
  output Q,
  output out_13,
  output nQ,
  output out_15,
  output Q_2,
  output out_17,
  output nQ_2,
  output Q_3,
  output nQ_3,
  output QA,
  output QB,
  output QC
);

  wire and_1_out, and_2_out, and_3_out, and_4_out, and_5_out, and_6_out, and_7_out, and_8_out, clock_1_out,
       clock_2_out, clock_3_out, clock_4_out, nand_1_out, nand_2_out, nand_3_out, nand_4_out, nand_7_out,
       nand_8_out, nand_9_out, nand_10_out, nor_4_out, nor_6_out, nor_8_out;

  Clock clock_1 (.out(clock_1_out));
  Clock clock_2 (.out(clock_2_out));
  nand nand_1 (nand_1_out, Data, clock_1_out);
  nand nand_2 (nand_2_out, clock_1_out, ~Data);  // NAND_Gate
  nand nand_3 (nand_3_out, out_15, J, clock_2_out);
  nand nand_4 (nand_4_out, clock_2_out, out_17);
  and and_1 (and_1_out, Q_3, K_2, clock_3_out);
  Clock clock_3 (.out(clock_3_out));
  and and_2 (and_2_out, clock_3_out, J_2, nQ_3);
  Flip_Flop_SR flip_flop_sr_1 (.S(nand_1_out), .R(nand_2_out), .Q(out_11), .nQ(out_13));
  nand nand_5 (out_15, nand_3_out, out_17);
  nand nand_6 (out_17, out_15, nand_4_out);
  nor nor_1 (Q_3, and_1_out, nQ_3);
  nor nor_2 (nQ_3, and_2_out, Q_3);
  Clock clock_4 (.out(clock_4_out));
  and and_3 (and_3_out, QA, 1'b1, clock_4_out);
  and and_4 (and_4_out, clock_4_out, 1'b1, nor_4_out);
  nor nor_3 (QA, and_3_out, nor_4_out);
  nor nor_4 (nor_4_out, and_4_out, QA);
  nand nand_7 (nand_7_out, D, EN);
  nand nand_8 (nand_8_out, EN, ~D);  // NAND_Gate
  nand nand_9 (nand_9_out, S, EN_2);
  nand nand_10 (nand_10_out, EN_2, R);
  or or_1 (Q, ~nand_7_out, ~nQ);  // OR_Gate
  or or_2 (nQ, ~Q, ~nand_8_out);  // OR_Gate
  or or_3 (Q_2, ~nand_9_out, ~nQ_2);  // OR_Gate
  or or_4 (nQ_2, ~Q_2, ~nand_10_out);  // OR_Gate
  and and_5 (and_5_out, QB, 1'b1, QA);
  and and_6 (and_6_out, QA, 1'b1, nor_6_out);
  nor nor_5 (QB, and_5_out, nor_6_out);
  nor nor_6 (nor_6_out, and_6_out, QB);
  and and_7 (and_7_out, QC, 1'b1, QB);
  and and_8 (and_8_out, QB, 1'b1, nor_8_out);
  nor nor_7 (QC, and_7_out, nor_8_out);
  nor nor_8 (nor_8_out, and_8_out, QC);

  // Notes on the sheet:
  //   Flip Flop D
  //   Flip Flop JK
  //   Flip Flop JK
  //   Latch D Controlado
  //   Latch SR Controlado
endmodule

module Flip_Flop_SR (
  input  S,
  input  R,
  output Q,
  output nQ
);

  nand nand_1 (Q, S, nQ);
  nand nand_2 (nQ, Q, R);
endmodule

module Flip_Flop_JK (
  input  K,
  input  CLK,
  input  J,
  output Q,
  output nQ
);

  wire and_1_out, and_2_out;

  and and_1 (and_1_out, Q, K, CLK);
  and and_2 (and_2_out, CLK, J, nQ);
  nor nor_1 (Q, and_1_out, nQ);
  nor nor_2 (nQ, and_2_out, Q);

  // Notes on the sheet:
  //   Flip Flop JK
endmodule
