// Logisim project Lista m3.circ as structural Verilog
module Banco_de_registradores (
  input  [31:0] Data,
  input  [3:0] R_addr,
  input  R_en,
  input  [3:0] W_addr,
  input  W_en,
  input  CLK,
  output [31:0] R_data
);

  wire and_1_out, and_2_out, and_3_out, and_4_out, and_5_out, and_6_out, and_7_out, and_8_out, and_9_out,
       and_10_out, and_11_out, and_12_out, and_13_out, and_14_out, and_15_out, and_16_out, decoder_1_out0,
       decoder_1_out1, decoder_1_out2, decoder_1_out3, decoder_1_out4, decoder_1_out5, decoder_1_out6,
       decoder_1_out7, decoder_1_out8, decoder_1_out9, decoder_1_out10, decoder_1_out11, decoder_1_out12,
       decoder_1_out13, decoder_1_out14, decoder_1_out15;
  wire [31:0] multiplexer_1_out, register_1_q, register_2_q, register_3_q, register_4_q, register_5_q,
       register_6_q, register_7_q, register_8_q, register_9_q, register_10_q;

  Decoder #(.select(4), .enable("false")) decoder_1 (
    .out0(decoder_1_out0), .out1(decoder_1_out1), .out2(decoder_1_out2), .out3(decoder_1_out3),
    .out4(decoder_1_out4), .out5(decoder_1_out5), .out6(decoder_1_out6), .out7(decoder_1_out7),
    .out8(decoder_1_out8), .out9(decoder_1_out9), .out10(decoder_1_out10), .out11(decoder_1_out11),
    .out12(decoder_1_out12), .out13(decoder_1_out13), .out14(decoder_1_out14), .out15(decoder_1_out15),
    .sel(W_addr));
  and and_1 (and_1_out, decoder_1_out0, W_en);
  and and_2 (and_2_out, decoder_1_out1, W_en);
  and and_3 (and_3_out, decoder_1_out2, W_en);
  and and_4 (and_4_out, decoder_1_out3, W_en);
  and and_5 (and_5_out, decoder_1_out4, W_en);
  and and_6 (and_6_out, decoder_1_out5, W_en);
  and and_7 (and_7_out, decoder_1_out6, W_en);
  and and_8 (and_8_out, decoder_1_out7, W_en);
  and and_9 (and_9_out, decoder_1_out8, W_en);
  and and_10 (and_10_out, decoder_1_out9, W_en);
  and and_11 (and_11_out, decoder_1_out10, W_en);
  and and_12 (and_12_out, decoder_1_out11, W_en);
  and and_13 (and_13_out, decoder_1_out12, W_en);
  and and_14 (and_14_out, decoder_1_out13, W_en);
  and and_15 (and_15_out, decoder_1_out14, W_en);
  and and_16 (and_16_out, decoder_1_out15, W_en);
  Register #(.width(32), .Select("low")) register_1 (
    .D(Data), .en(and_1_out), .Q(register_1_q), .clk(CLK));  // open: clr
  Register #(.width(32), .Select("low")) register_2 (
    .D(Data), .en(and_2_out), .Q(register_2_q), .clk(CLK));  // open: clr
  Register #(.width(32), .Select("low")) register_3 (
    .D(Data), .en(and_3_out), .Q(register_3_q), .clk(CLK));  // open: clr
  Register #(.width(32), .Select("low")) register_4 (
    .D(Data), .en(and_4_out), .Q(register_4_q), .clk(CLK));  // open: clr
  Register #(.width(32), .Select("low")) register_5 (
    .D(Data), .en(and_5_out), .Q(register_5_q), .clk(CLK));  // open: clr
  Register #(.width(32), .Select("low")) register_6 (
    .D(Data), .en(and_6_out), .Q(register_6_q), .clk(CLK));  // open: clr
  Register #(.width(32), .Select("low")) register_7 (
    .D(Data), .en(and_7_out), .Q(register_7_q), .clk(CLK));  // open: clr
  Register #(.width(32), .Select("low")) register_8 (
    .D(Data), .en(and_8_out), .Q(register_8_q), .clk(CLK));  // open: clr
  Register #(.width(32), .Select("low")) register_9 (
    .D(Data), .en(and_9_out), .Q(register_9_q), .clk(CLK));  // open: clr
  Register #(.width(32), .Select("low")) register_10 (
    .D(Data), .en(and_10_out), .Q(register_10_q), .clk(CLK));  // open: clr
  Register #(.width(32), .Select("low")) register_11 (.D(Data), .en(and_11_out), .clk(CLK));  // open: Q, clr
  Register #(.width(32), .Select("low")) register_12 (.D(Data), .en(and_12_out), .clk(CLK));  // open: Q, clr
  Register #(.width(32), .Select("low")) register_13 (.D(Data), .en(and_13_out), .clk(CLK));  // open: Q, clr
  Register #(.width(32), .Select("low")) register_14 (.D(Data), .en(and_14_out), .clk(CLK));  // open: Q, clr
  Register #(.width(32), .Select("low")) register_15 (.D(Data), .en(and_15_out), .clk(CLK));  // open: Q, clr
  Register #(.width(32), .Select("low")) register_16 (.D(Data), .en(and_16_out), .clk(CLK));  // open: Q, clr
  Multiplexer #(.select(4), .width(32), .enable("false")) multiplexer_1 (
    .in0(register_1_q), .in1(register_2_q), .in2(register_3_q), .in3(register_4_q), .in4(register_5_q),
    .in5(register_6_q), .in6(register_7_q), .in7(register_8_q), .in8(register_9_q), .in9(register_10_q),
    .out(multiplexer_1_out), .sel(R_addr));  // open: in10, in11, in12, in13, in14, in15
  Register #(.width(32), .Select("low")) register_17 (
    .D(multiplexer_1_out), .en(R_en), .Q(R_data), .clk(CLK));  // open: clr
endmodule

module ex_4_24_circuito_retrovisor_do_carro (
  input  [31:0] C,
  input  [3:0] WA,
  input  Load,
  input  [3:0] RA,
  output [31:0] Para_o_Display_do_retrovisor
);

  wire clock_1_out;

  Clock clock_1 (.out(clock_1_out));
  Banco_de_registradores banco_de_registradores_1 (
    .Data(C), .R_addr(RA), .R_en(1'b1), .W_addr(WA), .W_en(Load), .CLK(clock_1_out),
    .R_data(Para_o_Display_do_retrovisor));
endmodule

module ALU_8_bits (
  input  [7:0] A,
  input  [7:0] B,
  input  x,
  input  y,
  input  z,
  output [7:0] out_6
);

  wire alu_1_bit_1_cout, alu_1_bit_2_cout, alu_1_bit_3_cout, alu_1_bit_4_cout, alu_1_bit_5_cout,
       alu_1_bit_6_cout, alu_1_bit_last_bit_1_cout;

  Alu_1_bit_last_bit alu_1_bit_last_bit_1 (
    .z(z), .y(y), .x(x), .Cout(alu_1_bit_last_bit_1_cout), .Si(out_6[0]), .A(A[0]), .B(B[0]), .Cin(1'b0));
  ALU_1_bit alu_1_bit_1 (
    .z(z), .y(y), .x(x), .Cout(alu_1_bit_1_cout), .Si(out_6[1]), .A(A[1]), .B(B[1]),
    .Cin(alu_1_bit_last_bit_1_cout));
  ALU_1_bit alu_1_bit_2 (
    .z(z), .y(y), .x(x), .Cout(alu_1_bit_2_cout), .Si(out_6[2]), .A(A[2]), .B(B[2]), .Cin(alu_1_bit_1_cout));
  ALU_1_bit alu_1_bit_3 (
    .z(z), .y(y), .x(x), .Cout(alu_1_bit_3_cout), .Si(out_6[3]), .A(A[3]), .B(B[3]), .Cin(alu_1_bit_2_cout));
  ALU_1_bit alu_1_bit_4 (
    .z(z), .y(y), .x(x), .Cout(alu_1_bit_4_cout), .Si(out_6[4]), .A(A[4]), .B(B[4]), .Cin(alu_1_bit_3_cout));
  ALU_1_bit alu_1_bit_5 (
    .z(z), .y(y), .x(x), .Cout(alu_1_bit_5_cout), .Si(out_6[5]), .A(A[5]), .B(B[5]), .Cin(alu_1_bit_4_cout));
  ALU_1_bit alu_1_bit_6 (
    .z(z), .y(y), .x(x), .Cout(alu_1_bit_6_cout), .Si(out_6[6]), .A(A[6]), .B(B[6]), .Cin(alu_1_bit_5_cout));
  ALU_1_bit alu_1_bit_7 (.z(z), .y(y), .x(x), .Si(out_6[7]), .A(A[7]), .B(B[7]), .Cin(alu_1_bit_6_cout));  // open: Cout
endmodule

module ex_4_23_calculadora_usando_ALU (
  input  [7:0] A,
  input  [7:0] B,
  input  in_3,
  input  in_4,
  input  in_5,
  input  En,
  output [7:0] Saida
);

  wire Clk_out;
  wire [7:0] alu_8_bits_1_out_6;

  Clock Clk (.out(Clk_out));
  ALU_8_bits alu_8_bits_1 (.A(A), .B(B), .out_6(alu_8_bits_1_out_6), .x(in_3), .y(in_4), .z(in_5));
  Register #(.Select("low")) register_1 (.D(alu_8_bits_1_out_6), .en(En), .Q(Saida), .clk(Clk_out));  // open: clr
endmodule

module ALU_1_bit (
  input  Cin,
  input  A,
  input  B,
  input  z,
  input  y,
  input  x,
  output Cout,
  output Si
);

  wire adder_1_cout, adder_1_out, and_1_out, and_2_out, and_3_out, and_4_out, and_5_out, multiplexer_1_out,
       not_1_out, or_1_out, or_2_out, subtractor_1_bout, subtractor_1_out, xor_1_out, xor_2_out;

  xor xor_1 (xor_1_out, B, 1'b1);
  Multiplexer #(.select(3), .enable("false")) multiplexer_1 (
    .in0(B), .in1(xor_1_out), .in2(1'b0), .in3(1'b0), .out(multiplexer_1_out), .sel({x, y, z}));  // open: in4, in5, in6, in7
  and and_1 (and_1_out, 1'b1, ~x, ~y, z);  // AND_Gate
  or or_1 (or_1_out, and_1_out, Cin);
  Subtractor #(.width(1)) subtractor_1 (
    .a(A), .b(multiplexer_1_out), .out(subtractor_1_out), .bin(or_1_out), .bout(subtractor_1_bout));
  Adder #(.width(1)) adder_1 (.a(A), .b(multiplexer_1_out), .out(adder_1_out), .cin(or_1_out), .cout(adder_1_cout));
  and and_2 (and_2_out, A, B);
  or or_2 (or_2_out, A, B);
  xor xor_2 (xor_2_out, A, B);
  not not_1 (not_1_out, A);
  Multiplexer #(.select(3), .enable("false")) multiplexer_2 (
    .in0(adder_1_out), .in1(subtractor_1_out), .in2(adder_1_out), .in3(adder_1_out), .in4(and_2_out),
    .in5(or_2_out), .in6(xor_2_out), .in7(not_1_out), .out(Si), .sel({x, y, z}));
  and and_3 (and_3_out, ~x, ~y, z, subtractor_1_bout);  // AND_Gate
  and and_4 (and_4_out, adder_1_cout, ~x, ~y, ~z);  // AND_Gate
  and and_5 (and_5_out, adder_1_cout, ~x, y, ~z);  // AND_Gate
  or or_3 (Cout, and_3_out, and_4_out, and_5_out);
endmodule

module Alu_1_bit_last_bit (
  input  Cin,
  input  A,
  input  B,
  input  z,
  input  y,
  input  x,
  output Cout,
  output Si
);

  wire adder_1_cout, adder_1_out, and_1_out, and_2_out, and_3_out, and_4_out, and_5_out, multiplexer_1_out,
       not_1_out, or_1_out, or_2_out, subtractor_1_bout, subtractor_1_out, xor_1_out, xor_2_out;

  xor xor_1 (xor_1_out, B, 1'b1);
  Multiplexer #(.select(3), .enable("false")) multiplexer_1 (
    .in0(B), .in1(xor_1_out), .in2(1'b1), .in3(1'b0), .out(multiplexer_1_out), .sel({x, y, z}));  // open: in4, in5, in6, in7
  and and_1 (and_1_out, 1'b1, ~x, ~y, z);  // AND_Gate
  or or_1 (or_1_out, and_1_out, Cin);
  Adder #(.width(1)) adder_1 (.a(A), .b(multiplexer_1_out), .out(adder_1_out), .cin(or_1_out), .cout(adder_1_cout));
  and and_2 (and_2_out, A, B);
  or or_2 (or_2_out, A, B);
  xor xor_2 (xor_2_out, A, B);
  not not_1 (not_1_out, A);
  Subtractor #(.width(1)) subtractor_1 (
    .a(A), .b(multiplexer_1_out), .out(subtractor_1_out), .bin(or_1_out), .bout(subtractor_1_bout));
  Multiplexer #(.select(3), .enable("false")) multiplexer_2 (
    .in0(adder_1_out), .in1(subtractor_1_out), .in2(adder_1_out), .in3(adder_1_out), .in4(and_2_out),
    .in5(or_2_out), .in6(xor_2_out), .in7(not_1_out), .out(Si), .sel({x, y, z}));
  and and_3 (and_3_out, ~x, ~y, z, subtractor_1_bout);  // AND_Gate
  and and_4 (and_4_out, adder_1_cout, ~x, ~y, ~z);  // AND_Gate
  or or_3 (Cout, and_3_out, and_4_out, and_5_out);
  and and_5 (and_5_out, adder_1_cout, ~x, y, ~z);  // AND_Gate
endmodule

module ex_4_11_registrador_de_temperatura_4_ciclos (
  input  [7:0] T,
  input  En,
  input  [2:0] in_3,
  output [7:0] out_4
);

  wire adder_1_cout, adder_3_cout, Clk_out, or_1_out;
  wire [7:0] adder_1_out, adder_2_out, adder_3_out, register_1_q, register_2_q, register_3_q, register_4_q;

  Clock Clk (.out(Clk_out));
  Register #(.Select("low")) register_1 (.D(T), .en(En), .Q(register_1_q), .clk(Clk_out));  // open: clr
  Register #(.Select("low")) register_2 (.D(register_1_q), .en(En), .Q(register_2_q), .clk(Clk_out));  // open: clr
  Adder adder_1 (.a(register_1_q), .b(register_2_q), .out(adder_1_out), .cout(adder_1_cout));  // open: cin
  Register #(.Select("low")) register_3 (.D(register_2_q), .en(En), .Q(register_3_q), .clk(Clk_out));  // open: clr
  or or_1 (or_1_out, adder_1_cout, adder_3_cout);
  Adder adder_2 (.a(adder_1_out), .b(adder_3_out), .out(adder_2_out), .cin(or_1_out));  // open: cout
  Shifter #(.shift("lr")) shifter_1 (.in(adder_2_out), .\dist (in_3), .out(out_4));
  Register #(.Select("low")) register_4 (.D(register_3_q), .en(En), .Q(register_4_q), .clk(Clk_out));  // open: clr
  Adder adder_3 (.a(register_3_q), .b(register_4_q), .out(adder_3_out), .cout(adder_3_cout));  // open: cin
endmodule

module ex_fig_4_57_contador_com_carga_paralela (
  input  [3:0] L,
  input  ld,
  input  cnt,
  output [3:0] C,
  output [3:0] Tc
);

  wire clk_out, or_1_out;
  wire [3:0] adder_1_out, multiplexer_1_out;

  Clock clk (.out(clk_out));
  or or_1 (or_1_out, ld, cnt);
  assign Tc = C;  // AND_Gate and_1, 4 bits wide AND_Gate
  Multiplexer #(.width(4), .enable("false")) multiplexer_1 (
    .in0(adder_1_out), .in1(L), .out(multiplexer_1_out), .sel(ld));
  Register #(.width(4), .Select("low")) register_1 (
    .D(multiplexer_1_out), .en(or_1_out), .Q(C), .clk(clk_out));  // open: clr
  Adder #(.width(4)) adder_1 (.a(C), .b(4'b0001), .out(adder_1_out));  // open: cin, cout
endmodule

module conversor_RGB_CMY (
  input  [7:0] R,
  input  [7:0] G,
  input  [7:0] B,
  output [7:0] C,
  output [7:0] M,
  output [7:0] Y
);

  Subtractor subtractor_1 (.a({8{1'b1}}), .b(R), .out(C));  // open: bin, bout
  Subtractor subtractor_2 (.a({8{1'b1}}), .b(G), .out(M));  // open: bin, bout
  Subtractor subtractor_3 (.a({8{1'b1}}), .b(B), .out(Y));  // open: bin, bout
endmodule

module MIN (
  input  [7:0] A,
  input  [7:0] B,
  output [7:0] out_3
);

  wire comparator_1_gt;

  Comparator #(.width(9)) comparator_1 (.a({1'b0, A}), .b({1'b0, B}), .gt(comparator_1_gt));  // open: eq, lt
  Multiplexer #(.width(8), .enable("false")) multiplexer_1 (.in0(A), .in1(B), .out(out_3), .sel(comparator_1_gt));
endmodule

module ex_4_20_conversor_rgb_cmyk (
  input  [7:0] R,
  input  [7:0] G,
  input  [7:0] B,
  output [7:0] out_4,
  output [7:0] out_5,
  output [7:0] out_6,
  output [7:0] out_7
);

  wire [7:0] conversor_rgb_cmy_1_c, conversor_rgb_cmy_1_m, conversor_rgb_cmy_1_y, min_1_out_3;

  Subtractor subtractor_1 (.a(conversor_rgb_cmy_1_c), .b(out_7), .out(out_4));  // open: bin, bout
  conversor_RGB_CMY conversor_rgb_cmy_1 (
    .R(R), .G(G), .B(B), .C(conversor_rgb_cmy_1_c), .M(conversor_rgb_cmy_1_m), .Y(conversor_rgb_cmy_1_y));
  Subtractor subtractor_2 (.a(conversor_rgb_cmy_1_m), .b(out_7), .out(out_5));  // open: bin, bout
  MIN min_1 (.A(conversor_rgb_cmy_1_c), .B(conversor_rgb_cmy_1_m), .out_3(min_1_out_3));
  Subtractor subtractor_3 (.a(conversor_rgb_cmy_1_y), .b(out_7), .out(out_6));  // open: bin, bout
  MIN min_2 (.A(min_1_out_3), .B(conversor_rgb_cmy_1_y), .out_3(out_7));
endmodule
