// Logisim project M3 lista.circ as structural Verilog: 1 circuit, main circuit Balança com compensação de peso
module \Balança_com_compensação_de_peso  (
  input  [7:0] Sensor_de_Peso,
  input  [7:0] \Compensação ,
  output [7:0] out_3
);

  wire clock_1_out;
  wire [7:0] adder_1_out;

  Adder adder_1 (.a(Sensor_de_Peso), .b(\Compensação ), .out(adder_1_out));  // open: cin, cout
  Register #(.Select("low")) register_1 (.D(adder_1_out), .Q(out_3), .clk(clock_1_out));  // open: en, clr
  Clock clock_1 (.out(clock_1_out));
endmodule
