// Logisim project M5 - Implementação de Lógica Combinacional.circ as structural Verilog: 3 circuits, main circuit D4.8
module D4_8 (
  input  PortaMot,
  input  \Ignição ,
  input  Farol,
  output x
);

  wire and_1_out, and_2_out, not_1_out;

  not not_1 (not_1_out, \Ignição );
  and and_1 (and_1_out, not_1_out, Farol);
  and and_2 (and_2_out, PortaMot, \Ignição );
  or or_1 (x, and_1_out, and_2_out);

  // Notes on the sheet:
  //   Porta Aberta = 1
  //   Ignição Ligada = 1
  //   Farol Ligado = 1
endmodule

module BD_4_4_Nand (
  input  A,
  input  B,
  input  C,
  output x
);

  wire nand_1_out, nand_2_out, nand_3_out, nand_4_out, nand_5_out, nand_6_out, nand_7_out, nand_8_out;

  nand nand_1 (nand_1_out, ~A, ~C);  // NAND_Gate
  nand nand_2 (nand_2_out, ~B, ~C);  // NAND_Gate
  nand nand_3 (nand_3_out, B, C);
  nand nand_4 (nand_4_out, ~nand_1_out, ~nand_1_out);  // NAND_Gate
  nand nand_5 (nand_5_out, ~nand_2_out, ~nand_2_out);  // NAND_Gate
  nand nand_6 (nand_6_out, nand_4_out, nand_5_out);
  nand nand_7 (nand_7_out, nand_6_out, nand_6_out);
  nand nand_8 (nand_8_out, ~nand_3_out, ~nand_3_out);  // NAND_Gate
  nand nand_9 (x, nand_7_out, nand_8_out);
endmodule

module D4_5 (
  input  A,
  input  B,
  input  C,
  output x
);

  wire nand_1_out, nand_2_out, nand_3_out, nand_4_out, nand_5_out, nand_6_out, nand_7_out, nand_8_out;

  nand nand_1 (nand_1_out, ~A, ~B);  // NAND_Gate
  nand nand_2 (nand_2_out, ~A, ~C);  // NAND_Gate
  nand nand_3 (nand_3_out, ~B, ~C);  // NAND_Gate
  nand nand_4 (nand_4_out, ~nand_1_out, ~nand_1_out);  // NAND_Gate
  nand nand_5 (nand_5_out, ~nand_2_out, ~nand_2_out);  // NAND_Gate
  nand nand_6 (nand_6_out, nand_4_out, nand_5_out);
  nand nand_7 (nand_7_out, nand_6_out, nand_6_out);
  nand nand_8 (nand_8_out, ~nand_3_out, ~nand_3_out);  // NAND_Gate
  nand nand_9 (x, nand_7_out, nand_8_out);
endmodule
