// Logisim project M5 - Propriedade universal das portas NAND e NOR.circ as structural Verilog: 1 circuit, main circuit main
module main (
  input  in_1,
  input  in_2,
  input  in_3,
  input  in_4,
  input  in_5,
  output out_6
);

  wire nor_1_out, nor_2_out, nor_3_out, nor_4_out, nor_5_out, nor_6_out, nor_7_out, nor_8_out, nor_9_out;

  // Digital_Oscilloscope #(.nState(17)) digital_oscilloscope_1: pin names not known; wires that end beside it: in_5, in_1, in_2, in_3, in_4, out_6
  nor nor_1 (nor_1_out, in_1, in_2);
  nor nor_2 (nor_2_out, nor_1_out, nor_1_out);
  nor nor_3 (nor_3_out, in_3, in_3);
  nor nor_4 (nor_4_out, ~in_3, ~in_3);  // NOR_Gate
  nor nor_5 (nor_5_out, in_4, in_4);
  nor nor_6 (nor_6_out, nor_2_out, nor_3_out);
  nor nor_7 (nor_7_out, nor_6_out, nor_6_out);
  nor nor_8 (nor_8_out, nor_4_out, nor_5_out);
  nor nor_9 (nor_9_out, nor_8_out, nor_8_out);
  nor nor_10 (out_6, ~nor_7_out, ~nor_9_out);  // NOR_Gate

  // Other names for the same wires on the sheet: A = in_1; B = in_2; C = in_3; D = in_4; X = out_6
endmodule
