// Logisim project Multiplexador 8Bits.circ as structural Verilog: 2 circuits, main circuit main
module main (
  input  S0,
  input  S1,
  input  S2,
  input  E,
  input  D0,
  input  D1,
  input  D2,
  input  D3,
  input  D4,
  input  D5,
  input  D6,
  input  D7,
  output nOut,
  output Out
);

  wire and_1_out, and_2_out, and_3_out, and_4_out, and_5_out, and_6_out, and_7_out, and_8_out, not_1_out,
       not_2_out, not_3_out, not_4_out, not_5_out, not_6_out, not_7_out, or_1_out;

  not not_1 (not_1_out, S0);
  not not_2 (not_2_out, S1);
  not not_3 (not_3_out, S2);
  not not_4 (not_4_out, E);
  not not_5 (not_5_out, not_1_out);
  not not_6 (not_6_out, not_2_out);
  not not_7 (not_7_out, not_3_out);
  and and_1 (and_1_out, not_4_out, not_7_out, not_6_out, not_5_out, D7);
  and and_2 (and_2_out, not_4_out, not_3_out, not_6_out, not_5_out, D6);
  and and_3 (and_3_out, not_4_out, not_7_out, not_2_out, not_5_out, D5);
  and and_4 (and_4_out, not_4_out, not_3_out, not_2_out, not_5_out, D4);
  or or_1 (or_1_out, and_1_out, and_2_out, and_3_out, and_4_out, and_5_out, and_6_out, and_7_out, and_8_out);
  not not_8 (nOut, or_1_out);
  not not_9 (Out, nOut);
  and and_5 (and_5_out, not_4_out, not_7_out, not_6_out, not_1_out, D3);
  and and_6 (and_6_out, not_4_out, not_3_out, not_6_out, not_1_out, D2);
  and and_7 (and_7_out, not_4_out, not_7_out, not_2_out, not_1_out, D1);
  and and_8 (and_8_out, not_4_out, not_3_out, not_2_out, not_1_out, D0);
endmodule

module test (
  input  [2:0] in_1,
  input  in_2,
  input  in_3,
  input  in_4,
  input  in_5,
  input  in_6,
  input  in_7,
  input  in_8,
  input  in_9,
  input  in_10,
  output out_11,
  output out_12
);

  main main_1 (
    .S0(in_1[2]), .S1(in_1[1]), .S2(in_1[0]), .E(in_2), .D0(in_3), .D1(in_4), .D2(in_5), .D3(in_6),
    .D4(in_7), .D5(in_8), .D6(in_9), .D7(in_10), .nOut(out_11), .Out(out_12));
endmodule
