// Logisim project Multiplexador para Display de 7 segmentos.circ as structural Verilog: 1 circuit, main circuit main
module main (
  input  [3:0] in_1,
  input  [3:0] in_2
);

  wire a1, and_1_out, and_2_out, and_3_out, and_4_out, and_5_out, and_6_out, and_7_out, and_8_out, and_9_out,
       and_10_out, and_11_out, and_12_out, and_13_out, and_14_out, b1, c1, clock_1_out, D1, d1_t, D2, e1, f1,
       g1;
  wire [3:0] multiplexer_1_out;

  Multiplexer #(.width(4), .enable("false")) multiplexer_1 (
    .in0(in_1), .in1(in_2), .out(multiplexer_1_out), .sel(clock_1_out));
  Clock clock_1 (.out(clock_1_out));
  Decoder #(.enable("false")) decoder_1 (.out0(D1), .out1(D2), .sel(clock_1_out));
  // DisplayDecoder displaydecoder_1: pin names not known; wires that end beside it: multiplexer_1_out, a1, b1, c1, d1_t, e1, f1, g1
  and and_1 (and_1_out, g1, D1);
  and and_2 (and_2_out, f1, D1);
  _7_Segment_Display u_7_segment_display_1 (
    .g(and_1_out), .f(and_2_out), .a(and_6_out), .b(and_5_out), .e(and_3_out), .d(and_4_out), .c(and_7_out));  // open: dp
  and and_3 (and_3_out, e1, D1);
  and and_4 (and_4_out, d1_t, D1);
  and and_5 (and_5_out, b1, D1);
  and and_6 (and_6_out, a1, D1);
  and and_7 (and_7_out, c1, D1);
  and and_8 (and_8_out, f1, D2);
  and and_9 (and_9_out, g1, D2);
  _7_Segment_Display u_7_segment_display_2 (
    .g(and_9_out), .f(and_8_out), .a(and_12_out), .b(and_11_out), .e(and_10_out), .d(and_14_out),
    .c(and_13_out));  // open: dp
  and and_10 (and_10_out, e1, D2);
  and and_11 (and_11_out, b1, D2);
  and and_12 (and_12_out, a1, D2);
  and and_13 (and_13_out, c1, D2);
  and and_14 (and_14_out, d1_t, D2);

  // Other names for the same wires on the sheet: a2 = a1; b2 = b1; c2 = c1; d2_t = d1_t; e2 = e1; f2 = f1; g2 = g1
endmodule
