// Logisim project Multiplexadores.circ as structural Verilog: 1 circuit, main circuit main
module main (
  input  in_1,
  input  in_2,
  input  in_3,
  input  in_4,
  input  in_5,
  input  in_6,
  input  in_7,
  input  in_8,
  input  in_9,
  output out_10,
  output out_11,
  output out_12,
  output out_13
);

  wire and_1_out, and_2_out, and_3_out, and_4_out, and_5_out, and_6_out, and_7_out, and_8_out, and_9_out,
       and_10_out, and_11_out, and_12_out, and_13_out, nor_1_out, not_1_out, not_2_out, not_3_out, not_4_out,
       not_5_out, not_6_out, not_7_out, not_8_out, not_9_out, not_10_out, not_11_out, not_12_out, not_13_out;

  not not_1 (not_1_out, in_1);
  not not_2 (not_2_out, in_2);
  not not_3 (not_3_out, in_3);
  not not_4 (not_4_out, in_4);
  not not_5 (not_5_out, not_4_out);
  not not_6 (not_6_out, in_5);
  not not_7 (not_7_out, in_6);
  not not_8 (not_8_out, in_7);
  not not_9 (not_9_out, in_8);
  not not_10 (not_10_out, in_9);
  not not_11 (not_11_out, not_2_out);
  not not_12 (not_12_out, not_6_out);
  not not_13 (not_13_out, not_7_out);
  nor nor_1 (nor_1_out, not_9_out, not_10_out);
  nor nor_2 (out_13, not_9_out, not_10_out);
  and and_1 (and_1_out, not_1_out, not_11_out, not_5_out, not_13_out, nor_1_out);
  and and_2 (and_2_out, not_3_out, not_5_out, not_13_out, nor_1_out);
  and and_3 (and_3_out, not_6_out, not_13_out, nor_1_out);
  and and_4 (and_4_out, not_8_out, nor_1_out);
  buf and_5 (and_5_out, not_10_out);  // AND_Gate
  and and_6 (and_6_out, not_2_out, not_5_out, not_12_out, nor_1_out);
  and and_7 (and_7_out, not_3_out, not_5_out, not_12_out, nor_1_out);
  and and_8 (and_8_out, not_8_out, nor_1_out);
  and and_9 (and_9_out, not_8_out, nor_1_out);
  and and_10 (and_10_out, not_4_out, nor_1_out);
  and and_11 (and_11_out, not_6_out, nor_1_out);
  and and_12 (and_12_out, not_7_out, nor_1_out);
  and and_13 (and_13_out, not_8_out, nor_1_out);
  nor nor_3 (out_10, and_1_out, and_2_out, and_3_out, and_4_out, and_5_out);
  NotExactlyOne xnor_1 (.out(out_11), .in0(and_6_out), .in1(and_7_out), .in2(and_8_out), .in3(and_9_out));
  NotExactlyOne xnor_2 (.out(out_12), .in0(and_10_out), .in1(and_11_out), .in2(and_12_out), .in3(and_13_out));
endmodule
