// Logisim project Portas logicas transistores.circ as structural Verilog: 1 circuit, main circuit main
module main (
  input  S,
  input  X,
  input  Y,
  input  K,
  input  in_5,
  input  in_6,
  output O,
  output W,
  output out_9
);

  wire transistor_1_out, transistor_2_out, transistor_6_out, transistor_9_out, transistor_10_out,
       transistor_14_out;

  Transistor transistor_1 (.in(1'b1), .out(transistor_1_out), .gate(X));
  Transistor transistor_2 (.in(1'b1), .out(transistor_2_out), .gate(in_5));
  Transistor transistor_3 (.in(transistor_2_out), .out(out_9), .gate(in_6));
  Transistor #(.gate("br")) transistor_4 (.in(1'b1), .out(transistor_1_out), .gate(Y));
  Transistor #(.\type ("n")) transistor_5 (.in(transistor_6_out), .out(transistor_1_out), .gate(X));
  Transistor #(.\type ("n")) transistor_6 (.in(1'b0), .out(transistor_6_out), .gate(Y));
  Transistor transistor_7 (.in(1'b1), .out(O), .gate(transistor_1_out));
  Transistor #(.\type ("n")) transistor_8 (.in(1'b0), .out(O), .gate(transistor_1_out));
  Transistor transistor_9 (.in(1'b1), .out(transistor_9_out), .gate(S));
  Transistor #(.\type ("n")) transistor_10 (.in(transistor_9_out), .out(transistor_10_out), .gate(S));
  Transistor transistor_11 (.in(1'b0), .out(W), .gate(transistor_9_out));
  Transistor #(.gate("br")) transistor_12 (.in(1'b0), .out(W), .gate(K));
  Transistor #(.\type ("n")) transistor_13 (.in(transistor_14_out), .out(W), .gate(transistor_9_out));
  Transistor #(.\type ("n")) transistor_14 (.in(1'b1), .out(transistor_14_out), .gate(K));
  // also tied to GND on the sheet: transistor_10_out

  // Notes on the sheet:
  //   AND
  //   NOR
endmodule
