// Logisim project R4 - Análise booleana de circuitos lógicos. .circ as structural Verilog: 2 circuits, main circuit main
module main (
  input  in_1,
  input  in_2,
  input  in_3,
  input  in_4,
  output out_5
);

  wire and_1_out, or_1_out;

  or or_1 (or_1_out, in_1, in_2);
  and and_1 (and_1_out, or_1_out, in_3);
  or or_2 (out_5, and_1_out, in_4);

  // Other names for the same wires on the sheet: A = in_4; B = in_3; C = in_2; D = in_1
endmodule

module main2 (
  input  a,
  input  b,
  input  c,
  input  d,
  output x
);

  wire and_1_out, or_1_out;

  or or_1 (or_1_out, d, c);
  and and_1 (and_1_out, or_1_out, b);
  or or_2 (x, and_1_out, a);
endmodule
