// Logisim project R4 - Procedimento de projeto de circuitos logicos combinacionais.circ as structural Verilog: 2 circuits, main circuit main
module main (
  input  in_1,
  input  in_2,
  input  in_3,
  output out_4
);

  wire and_1_out, and_2_out, and_3_out;

  and and_1 (and_1_out, in_1, in_2);
  and and_2 (and_2_out, in_3, in_2);
  and and_3 (and_3_out, in_3, in_1);
  or or_1 (out_4, and_1_out, and_2_out, and_3_out);

  // Other names for the same wires on the sheet: A = in_3; B = in_1; C = in_2
endmodule

module exemplo_4_7 (
  input  A,
  input  B,
  input  C,
  output x
);

  wire nand_1_out, nand_2_out, nand_3_out;

  nand nand_1 (nand_1_out, B, C);
  nand nand_2 (nand_2_out, A, C);
  nand nand_3 (nand_3_out, A, B);
  nand nand_4 (x, nand_1_out, nand_2_out, nand_3_out);
endmodule
