// Logisim project R4 - Simplificação usando álgebra booleana .circ as structural Verilog: 1 circuit, main circuit main
module main (
  input  in_1,
  input  in_2,
  input  in_3,
  output out_4
);

  wire and_1_out, and_2_out, and_3_out, and_4_out, nor_1_out, or_1_out, or_2_out, xor_1_out;

  and and_1 (and_1_out, in_1, in_2);
  and and_2 (and_2_out, in_1, in_3);
  and and_3 (and_3_out, ~in_2, ~in_3);  // AND_Gate
  nor nor_1 (nor_1_out, and_1_out, and_2_out);
  and and_4 (and_4_out, ~in_1, ~in_2, in_3);  // AND_Gate
  or or_1 (or_1_out, ~in_1, and_3_out);  // OR_Gate
  or or_2 (or_2_out, nor_1_out, and_4_out);
  not not_1 (out_4, xor_1_out);
  xor xor_1 (xor_1_out, or_2_out, or_1_out);

  // Other names for the same wires on the sheet: A = in_1; B = in_2; C = in_3
endmodule
