// Logisim project RAM.circ as structural Verilog
module main (
  input  [7:0] in_1,
  input  in_2,
  input  [7:0] in_3,
  input  in_4,
  output [7:0] out_5,
  output [31:0] out_6,
  output out_7,
  output [7:0] out_8,
  output [7:0] out_9,
  output [7:0] out_10
);

  wire bloco_operacional_sad_1_i_lt_256, button_1_out, clk, clock_1_out, comparator_1_eq, contador_2_1_rco,
       controle_sad_1_i_clr, controle_sad_1_i_inc, controle_sad_1_sad_reg_ld, controle_sad_1_sina_ld,
       controle_sad_1_soma_clr, inicia_contagem_1_y, not_1_out, not_2_out, not_3_out;

  ButtonSync buttonsync_1 (.bi(contador_2_1_rco), .Clk(clk), .bo(out_7));
  contador_2 contador_2_1 (.CLK(clk), .En(1'b1), .CLR(button_1_out), .Y(out_9[3:0]), .RCO(contador_2_1_rco));
  contador_2 contador_2_2 (.CLK(clk), .En(contador_2_1_rco), .CLR(button_1_out), .Y(out_9[7:4]));  // open: RCO
  Comparator comparator_1 (.a(out_9), .b({8{1'b1}}), .eq(comparator_1_eq));  // open: gt, lt
  inicia_contagem inicia_contagem_1 (
    .X(comparator_1_eq), .restart(button_1_out), .clk(out_8[0]), .Y(inicia_contagem_1_y));
  not not_1 (not_1_out, inicia_contagem_1_y);
  Multiplexer #(.enable("false")) multiplexer_1 (.in0(out_8[0]), .in1(1'b0), .out(clk), .sel(not_1_out));
  assign out_5 = not_2_out ? in_1 : 8'bz;  // Controlled_Buffer controlled_buffer_1
  not not_2 (not_2_out, 1'b1);
  RAM #(.Select("low")) ram_1 (.addr(out_9), .data(out_5), .sel(in_2), .clk(clk), .ld(1'b1));  // open: clr
  assign out_10 = not_3_out ? in_3 : 8'bz;  // Controlled_Buffer controlled_buffer_2
  not not_3 (not_3_out, 1'b1);
  Button button_1 (.out(button_1_out));
  RAM #(.Select("low")) ram_2 (.addr(out_9), .data(out_10), .sel(in_4), .clk(clk), .ld(1'b1));  // open: clr
  Clock clock_1 (.out(clock_1_out));
  controle_SAD controle_sad_1 (
    .comece(button_1_out), .i_lt_256(bloco_operacional_sad_1_i_lt_256), .i_clr(controle_sad_1_i_clr),
    .soma_clr(controle_sad_1_soma_clr), .sina_ld(controle_sad_1_sina_ld), .i_inc(controle_sad_1_i_inc),
    .sad_reg_ld(controle_sad_1_sad_reg_ld), .CLK(clock_1_out));  // open: AB_rd
  Bloco_operacional_SAD bloco_operacional_sad_1 (
    .A_dados(out_5), .B_dados(out_10), .i_clr(controle_sad_1_i_clr), .clk(clock_1_out),
    .soma_ld(controle_sad_1_sina_ld), .soma_clr(controle_sad_1_soma_clr),
    .sad_reg_ld(controle_sad_1_sad_reg_ld), .i_lt_256(bloco_operacional_sad_1_i_lt_256), .sad(out_6),
    .AB_end(out_8), .i_inc(controle_sad_1_i_inc), .sad_reg_clr(button_1_out));

  // Other names for the same wires on the sheet: clk2 = out_8[0]
endmodule

module ButtonSync (
  input  bi,
  input  Clk,
  output bo
);

  wire and_1_out, and_2_out, not_1_out, not_2_out, not_3_out, not_4_out, not_5_out;
  wire [1:0] and_3_out, register_1_q;

  not not_1 (not_1_out, register_1_q[1]);
  not not_2 (not_2_out, register_1_q[0]);
  not not_3 (not_3_out, register_1_q[1]);
  not not_4 (not_4_out, register_1_q[0]);
  not not_5 (not_5_out, register_1_q[1]);
  and and_1 (and_1_out, not_1_out, register_1_q[0], bi);
  and and_2 (and_2_out, register_1_q[1], not_2_out, bi);
  and and_3 (and_3_out[0], not_3_out, not_4_out, bi);
  and and_4 (bo, not_5_out, register_1_q[0]);
  Register #(.width(2), .Select("low")) register_1 (.D(and_3_out), .Q(register_1_q), .clk(Clk));  // open: en, clr
  or or_1 (and_3_out[1], and_1_out, and_2_out);
endmodule

module contador_2 (
  input  CLK,
  input  En,
  input  CLR,
  output [3:0] Y,
  output RCO
);

  wire and_1_out, CLK_t;

  Multiplexer #(.enable("false")) multiplexer_1 (.in0(1'b1), .in1(CLK), .out(CLK_t), .sel(En));
  J_K_Flip_Flop #(.trigger("falling")) j_k_ff_1 (
    .J(1'b1), .clk(CLK_t), .K(1'b1), .Q(Y[0]), .reset(CLR));  // open: Qn, preset
  J_K_Flip_Flop #(.trigger("falling")) j_k_ff_2 (
    .J(1'b1), .clk(Y[0]), .K(1'b1), .Q(Y[1]), .reset(CLR));  // open: Qn, preset
  J_K_Flip_Flop #(.trigger("falling")) j_k_ff_3 (
    .J(1'b1), .clk(Y[1]), .K(1'b1), .Q(Y[2]), .reset(CLR));  // open: Qn, preset
  J_K_Flip_Flop #(.trigger("falling")) j_k_ff_4 (
    .J(1'b1), .clk(Y[2]), .K(1'b1), .Q(Y[3]), .reset(CLR));  // open: Qn, preset
  Register #(.width(1), .Select("low")) register_1 (.D(and_1_out), .Q(RCO), .clk(CLK_t));  // open: en, clr
  and and_1 (and_1_out, Y[3], Y[2], Y[1], Y[0]);
endmodule

module controle_SAD (
  input  comece,
  input  i_lt_256,
  input  CLK,
  output i_clr,
  output soma_clr,
  output sina_ld,
  output AB_rd,
  output i_inc,
  output sad_reg_ld
);

  wire and_4_out, and_8_out, and_9_out, not_1_out, not_2_out, not_3_out, not_4_out, not_5_out, not_6_out,
       not_7_out, not_8_out, not_9_out;
  wire [1:0] register_1_q;
  wire [2:0] or_2_out;

  not not_1 (not_1_out, sad_reg_ld);
  not not_2 (not_2_out, register_1_q[1]);
  not not_3 (not_3_out, register_1_q[1]);
  and and_1 (sina_ld, register_1_q[1], register_1_q[0]);
  and and_2 (AB_rd, register_1_q[1], register_1_q[0]);
  and and_3 (i_inc, register_1_q[1], register_1_q[0]);
  not not_4 (not_4_out, register_1_q[0]);
  not not_5 (not_5_out, i_lt_256);
  and and_4 (and_4_out, register_1_q[1], i_lt_256);
  not not_6 (not_6_out, sad_reg_ld);
  not not_7 (not_7_out, register_1_q[1]);
  not not_8 (not_8_out, register_1_q[0]);
  not not_9 (not_9_out, register_1_q[0]);
  Register #(.width(3), .Select("low")) register_1 (
    .D(or_2_out), .Q({sad_reg_ld, register_1_q}), .clk(CLK));  // open: en, clr
  and and_5 (i_clr, not_1_out, not_2_out, register_1_q[0]);
  and and_6 (soma_clr, not_3_out, register_1_q[0]);
  and and_7 (or_2_out[2], register_1_q[1], not_4_out, not_5_out);
  or or_1 (or_2_out[1], register_1_q[0], and_4_out);
  and and_8 (and_8_out, not_6_out, not_7_out, not_8_out, comece);
  and and_9 (and_9_out, register_1_q[1], not_9_out, i_lt_256);
  or or_2 (or_2_out[0], and_8_out, and_9_out);
endmodule

module Bloco_operacional_SAD (
  input  [7:0] A_dados,
  input  [7:0] B_dados,
  input  i_inc,
  input  i_clr,
  input  clk,
  input  soma_ld,
  input  soma_clr,
  input  sad_reg_ld,
  input  sad_reg_clr,
  output [7:0] AB_end,
  output i_lt_256,
  output [31:0] sad
);

  wire comparator_1_eq, comparator_2_eq, comparator_2_lt, or_1_out;
  wire [7:0] adder_1_out, multiplexer_1_out, multiplexer_2_out, subtractor_1_out;
  wire [31:0] adder_2_out, soma_q;

  Adder adder_1 (.a(AB_end), .b(8'h1), .out(adder_1_out));  // open: cin, cout
  Register #(.Select("low")) i (.D(adder_1_out), .en(i_inc), .Q(AB_end), .clk(clk), .clr(i_clr));
  not not_1 (i_lt_256, comparator_1_eq);
  Comparator #(.mode("unsigned")) comparator_1 (.a(AB_end), .b({8{1'b1}}), .eq(comparator_1_eq));  // open: gt, lt
  Register #(.width(32), .Select("low")) soma (.D(adder_2_out), .en(soma_ld), .Q(soma_q), .clk(clk), .clr(soma_clr));
  Comparator #(.mode("unsigned")) comparator_2 (
    .a(A_dados), .b(B_dados), .eq(comparator_2_eq), .lt(comparator_2_lt));  // open: gt
  Register #(.width(32), .Select("low")) sad_reg (
    .D(soma_q), .Q(sad), .clk(clk), .clr(sad_reg_clr), .cs(sad_reg_ld));  // open: en, preset
  or or_1 (or_1_out, comparator_2_eq, comparator_2_lt);
  Multiplexer #(.width(8), .enable("false")) multiplexer_1 (
    .in0(A_dados), .in1(B_dados), .out(multiplexer_1_out), .sel(or_1_out));
  Multiplexer #(.width(8), .enable("false")) multiplexer_2 (
    .in0(B_dados), .in1(A_dados), .out(multiplexer_2_out), .sel(or_1_out));
  Subtractor subtractor_1 (.a(multiplexer_1_out), .b(multiplexer_2_out), .out(subtractor_1_out));  // open: bin, bout
  Adder #(.width(32)) adder_2 (.a({{24{1'b0}}, subtractor_1_out}), .b(soma_q), .out(adder_2_out));  // open: cin, cout
endmodule

module inicia_contagem (
  input  X,
  input  restart,
  input  clk,
  output Y
);

  wire and_1_out, and_2_out, not_2_out, not_3_out, or_1_out, register_1_q;

  not not_1 (Y, register_1_q);
  not not_2 (not_2_out, register_1_q);
  and and_1 (and_1_out, not_2_out, X);
  and and_2 (and_2_out, register_1_q, not_3_out);
  not not_3 (not_3_out, restart);
  Register #(.width(1), .Select("low")) register_1 (.D(or_1_out), .Q(register_1_q), .clk(clk));  // open: en, clr
  or or_1 (or_1_out, and_1_out, and_2_out);
endmodule
