// Logisim project Rtl ex 5.6.circ as structural Verilog: 5 circuits, main circuit Bloco Operacional
module Bloco_Operacional (
  input  Q1_ld,
  input  [3:0] A,
  input  [3:0] Faddr,
  input  [31:0] Q,
  input  Clk,
  input  D_en,
  output A_eq_Faddr,
  output [31:0] D
);

  wire [31:0] register_1_q;

  Comparador comparador_1 (.A(A), .B(Faddr), .out_3(A_eq_Faddr));
  Register #(.width(32), .Select("low")) register_1 (.D(Q), .en(Q1_ld), .Q(register_1_q), .clk(Clk));  // open: clr
  Driver driver_1 (.Q1(register_1_q), .Den(D_en), .Clk(Clk), .D(D));
endmodule

module Comparador (
  input  [3:0] A,
  input  [3:0] B,
  output out_3
);

  Comparator #(.width(5)) comparator_1 (
    .a({1'b0, A[3], A[0], A[1], A[2]}), .b({1'b0, B[3], B[0], B[1], B[2]}), .eq(out_3));  // open: gt, lt
endmodule

module Driver (
  input  [31:0] Q1,
  input  Den,
  input  Clk,
  output [31:0] D
);

  Register #(.width(32), .Select("low")) register_1 (.D(Q1), .en(Den), .Q(D), .clk(Clk));  // open: clr
endmodule

module Bloco_de_controle (
  input  rd,
  input  A_eq_Faddr,
  input  clk,
  output D_en,
  output Q1_ld
);

  wire and_1_out;

  not not_1 (Q1_ld, D_en);
  and and_1 (and_1_out, rd, A_eq_Faddr);
  Register #(.width(1), .Select("low")) register_1 (.D(and_1_out), .Q(D_en), .clk(clk));  // open: en, clr
endmodule

module circuito (
  input  [31:0] Q,
  input  in_2,
  input  [3:0] in_3,
  input  [3:0] in_4,
  output [31:0] D
);

  wire bloco_de_controle_1_d_en, bloco_de_controle_1_q1_ld, bloco_operacional_1_a_eq_faddr, clock_1_out;

  Clock clock_1 (.out(clock_1_out));
  Bloco_de_controle bloco_de_controle_1 (
    .D_en(bloco_de_controle_1_d_en), .Q1_ld(bloco_de_controle_1_q1_ld), .rd(in_2),
    .A_eq_Faddr(bloco_operacional_1_a_eq_faddr), .clk(clock_1_out));
  Bloco_Operacional bloco_operacional_1 (
    .Q1_ld(bloco_de_controle_1_q1_ld), .Clk(clock_1_out), .A_eq_Faddr(bloco_operacional_1_a_eq_faddr),
    .A(in_4), .Faddr(in_3), .Q(Q), .D(D), .D_en(bloco_de_controle_1_d_en));
endmodule
