// Logisim project Tabela verdade Portas logicas.circ as structural Verilog: 1 circuit, main circuit main
module main (
  input  in_1,
  input  in_2,
  input  in_3,
  input  in_4,
  input  in_5,
  input  in_6,
  input  in_7,
  input  in_8,
  input  in_9,
  input  in_10,
  input  in_11,
  input  in_12,
  input  in_13,
  input  in_14,
  input  in_15,
  input  in_16,
  input  in_17
);

  wire and_2_out, button_1_out, button_2_out, button_6_out, button_7_out, digital_oscilloscope_1_p4,
       digital_oscilloscope_2_p1, digital_oscilloscope_2_p4, digital_oscilloscope_2_p5,
       digital_oscilloscope_3_p1, digital_oscilloscope_3_p4, digital_oscilloscope_4_p1,
       digital_oscilloscope_5_p4, nor_1_out, or_1_out;

  Button button_1 (.out(button_1_out));
  // Digital_Oscilloscope #(.nState(12)) digital_oscilloscope_1: pin names not known; wires that end beside it: button_1_out, in_1, in_2, digital_oscilloscope_1_p4
  or or_1 (or_1_out, in_8, in_9, in_10);
  Button button_2 (.out(button_2_out));
  // Digital_Oscilloscope #(.nState(12)) digital_oscilloscope_2: pin names not known; wires that end beside it: digital_oscilloscope_2_p1, in_16, in_17, digital_oscilloscope_2_p4, digital_oscilloscope_2_p5
  Button button_3 (.out(digital_oscilloscope_2_p1));
  // Digital_Oscilloscope digital_oscilloscope_3: pin names not known; wires that end beside it: digital_oscilloscope_3_p1, in_6, in_7, digital_oscilloscope_3_p4
  Button button_4 (.out(digital_oscilloscope_3_p1));
  // Digital_Oscilloscope #(.nState(21)) digital_oscilloscope_4: pin names not known; wires that end beside it: digital_oscilloscope_4_p1, in_8, in_9, in_10, or_1_out
  Button button_5 (.out(digital_oscilloscope_4_p1));
  // Digital_Oscilloscope #(.nState(12)) digital_oscilloscope_5: pin names not known; wires that end beside it: button_2_out, in_11, in_12, digital_oscilloscope_5_p4
  nor nor_1 (nor_1_out, in_13, in_14, in_15);
  Button button_6 (.out(button_6_out));
  // Digital_Oscilloscope #(.nState(8)) digital_oscilloscope_6: pin names not known; wires that end beside it: button_6_out, in_13, in_14, in_15, nor_1_out
  and and_1 (digital_oscilloscope_1_p4, in_1, in_2);
  nand nand_1 (digital_oscilloscope_5_p4, in_11, in_12);
  xnor xnor_1 (digital_oscilloscope_2_p5, in_16, in_17);
  xor xor_1 (digital_oscilloscope_2_p4, in_16, in_17);
  and and_2 (and_2_out, in_3, in_4, in_5);
  Button button_7 (.out(button_7_out));
  // Digital_Oscilloscope #(.nState(20)) digital_oscilloscope_7: pin names not known; wires that end beside it: button_7_out, in_3, in_4, in_5, and_2_out
  or or_2 (digital_oscilloscope_3_p4, in_6, in_7);
endmodule
