// Logisim project display 7 seg.circ as structural Verilog: 1 circuit, main circuit main
module main (
);

  wire and_1_out, and_2_out, and_3_out, nand_1_out, nand_2_out, nand_3_out, nand_4_out, nand_5_out,
       nand_6_out, nand_7_out, nand_8_out, nand_9_out, nand_10_out, nand_11_out, nand_12_out, nand_13_out,
       nand_14_out, nand_15_out, nand_16_out, nand_17_out, nand_18_out, nand_19_out, nand_20_out, nand_21_out;

  // NAND_Gate nand_1 has open pins: out=nand_1_out
  // NAND_Gate nand_2 has open pins: out=nand_2_out
  // NAND_Gate nand_3 has open pins: out=nand_3_out
  // NAND_Gate nand_4 has open pins: out=nand_4_out
  // NAND_Gate nand_5 has open pins: out=nand_5_out
  // NAND_Gate nand_6 has open pins: out=nand_6_out
  // NAND_Gate nand_7 has open pins: out=nand_7_out
  // NAND_Gate nand_8 has open pins: out=nand_8_out
  // NAND_Gate nand_9 has open pins: out=nand_9_out
  // NAND_Gate nand_10 has open pins: out=nand_10_out
  // NAND_Gate nand_11 has open pins: out=nand_11_out
  // NAND_Gate nand_12 has open pins: out=nand_12_out
  // NAND_Gate nand_13 has open pins: out=nand_13_out
  // NAND_Gate nand_14 has open pins: out=nand_14_out
  // NAND_Gate nand_15 has open pins: out=nand_15_out
  // NAND_Gate nand_16 has open pins: out=nand_16_out
  // NAND_Gate nand_17 has open pins: out=nand_17_out
  // NAND_Gate nand_18 has open pins: out=nand_18_out
  // NAND_Gate nand_19 has open pins: out=nand_19_out
  // NAND_Gate nand_20 has open pins: out=nand_20_out
  // NAND_Gate nand_21 has open pins: out=nand_21_out
  and and_1 (and_1_out, nand_1_out, nand_2_out, nand_3_out, nand_4_out);
  and and_2 (and_2_out, nand_5_out, nand_6_out, nand_7_out, nand_8_out);
  and and_3 (and_3_out, nand_19_out, nand_20_out, nand_21_out);
  // AND_Gate and_4 has open pins: in0=and_1_out, in1=and_2_out, in2=and_3_out, in3=nand_9_out, in4=nand_10_out, in5=nand_11_out, in6=nand_12_out, in7=nand_13_out, in8=nand_14_out, in9=nand_15_out, in10=nand_16_out, in11=nand_17_out, in12=nand_18_out, out=open
endmodule
