// Logisim project ex 3.7,9,10,11,13.circ as structural Verilog: 6 circuits, main circuit main
module main (
  output r
);

  wire and_1_out, and_2_out, and_3_out, and_5_out, and_6_out, and_7_out, and_8_out, button_1_out,
       clock_1_out, digital_oscilloscope_1_p1, not_1_out, not_2_out, not_3_out, not_4_out, not_5_out,
       not_6_out, not_7_out, not_8_out, not_9_out, not_10_out, not_11_out, not_12_out, not_13_out,
       not_14_out, not_15_out;
  wire [2:0] or_3_out, register_1_q;

  Button button_1 (.out(button_1_out));
  not not_1 (not_1_out, register_1_q[2]);
  not not_2 (not_2_out, register_1_q[1]);
  not not_3 (not_3_out, register_1_q[2]);
  not not_4 (not_4_out, register_1_q[0]);
  not not_5 (not_5_out, register_1_q[1]);
  not not_6 (not_6_out, register_1_q[0]);
  not not_7 (not_7_out, register_1_q[2]);
  not not_8 (not_8_out, register_1_q[2]);
  not not_9 (not_9_out, register_1_q[1]);
  not not_10 (not_10_out, register_1_q[2]);
  not not_11 (not_11_out, register_1_q[0]);
  not not_12 (not_12_out, register_1_q[2]);
  not not_13 (not_13_out, register_1_q[0]);
  not not_14 (not_14_out, register_1_q[2]);
  not not_15 (not_15_out, register_1_q[0]);
  Register #(.width(3), .Select("low")) register_1 (
    .D(or_3_out), .Q(register_1_q), .clk(clock_1_out));  // open: en, clr
  Clock clock_1 (.out(clock_1_out));
  and and_1 (and_1_out, not_1_out, not_2_out, register_1_q[0]);
  and and_2 (and_2_out, not_3_out, register_1_q[1], not_4_out);
  and and_3 (and_3_out, register_1_q[2], not_5_out, not_6_out);
  and and_4 (or_3_out[2], not_7_out, register_1_q[1], register_1_q[0]);
  and and_5 (and_5_out, not_8_out, not_9_out, register_1_q[0]);
  and and_6 (and_6_out, not_10_out, register_1_q[1], not_11_out);
  and and_7 (and_7_out, not_12_out, not_13_out, button_1_out);
  and and_8 (and_8_out, not_14_out, register_1_q[1], not_15_out);
  or or_1 (r, and_1_out, and_2_out, and_3_out);
  or or_2 (or_3_out[1], and_5_out, and_6_out);
  or or_3 (or_3_out[0], and_7_out, and_8_out);
  // Digital_Oscilloscope #(.nState(8)) digital_oscilloscope_1: pin names not known; wires that end beside it: digital_oscilloscope_1_p1, button_1_out, r
  Clock clock_2 (.out(digital_oscilloscope_1_p1));
endmodule

module main_2 (
  output [3:0] out_1
);

  wire and_3_out, and_4_out, clock_1_out, not_1_out, not_2_out, not_4_out, not_5_out;
  wire [0:0] register_1_q;
  wire [1:0] not_6_out;

  not not_1 (not_1_out, register_1_q[0]);
  not not_2 (not_2_out, out_1[3]);
  not not_3 (out_1[0], out_1[3]);
  not not_4 (not_4_out, out_1[3]);
  not not_5 (not_5_out, register_1_q[0]);
  not not_6 (not_6_out[0], register_1_q[0]);
  and and_1 (out_1[2], out_1[3], not_1_out);
  and and_2 (out_1[1], not_2_out, register_1_q[0]);
  and and_3 (and_3_out, not_4_out, register_1_q[0]);
  and and_4 (and_4_out, out_1[3], not_5_out);
  Register #(.width(2), .Select("low")) register_1 (
    .D(not_6_out), .Q({out_1[3], register_1_q[0]}), .clk(clock_1_out));  // open: en, clr
  Clock clock_1 (.out(clock_1_out));
  or or_1 (not_6_out[1], and_3_out, and_4_out);
  // Digital_Oscilloscope #(.nState(5)) digital_oscilloscope_1: pin names not known; wires that end beside it: clock_1_out, out_1[3], out_1[2], out_1[1], out_1[0]

  // Notes on the sheet:
  //   W
  //   X
  //   Y
  //   Z
  //   CLK
endmodule

module ex_3_7 (
  output x
);

  wire and_1_out, and_2_out, and_3_out, and_4_out, and_5_out, B, clock_1_out, clock_2_out, not_1_out,
       not_2_out, not_3_out, not_4_out, not_5_out;
  wire [1:0] or_3_out, register_1_q;

  Button button_1 (.out(B));
  or or_1 (x, register_1_q[0], register_1_q[1]);
  not not_1 (not_1_out, register_1_q[1]);
  not not_2 (not_2_out, register_1_q[1]);
  not not_3 (not_3_out, register_1_q[0]);
  not not_4 (not_4_out, register_1_q[0]);
  not not_5 (not_5_out, register_1_q[0]);
  Clock clock_1 (.out(clock_1_out));
  and and_1 (and_1_out, not_1_out, B);
  and and_2 (and_2_out, not_2_out, register_1_q[0]);
  and and_3 (and_3_out, register_1_q[1], not_3_out);
  and and_4 (and_4_out, not_4_out, B);
  and and_5 (and_5_out, register_1_q[1], not_5_out);
  Register #(.width(2), .Select("low")) register_1 (
    .D(or_3_out), .Q(register_1_q), .clk(clock_1_out));  // open: en, clr
  or or_2 (or_3_out[1], and_1_out, and_2_out, and_3_out);
  or or_3 (or_3_out[0], and_4_out, and_5_out);
  Clock clock_2 (.out(clock_2_out));
  // Digital_Oscilloscope digital_oscilloscope_1: pin names not known; wires that end beside it: clock_2_out, B, x
endmodule

module ex_3_10 (
  output [3:0] out_1
);

  wire and_3_out, and_4_out, clock_1_out, not_1_out, not_2_out, not_4_out, not_5_out;
  wire [0:0] register_1_q;
  wire [1:0] not_6_out;

  not not_1 (not_1_out, register_1_q[0]);
  not not_2 (not_2_out, out_1[3]);
  not not_3 (out_1[0], out_1[3]);
  not not_4 (not_4_out, out_1[3]);
  not not_5 (not_5_out, register_1_q[0]);
  not not_6 (not_6_out[0], register_1_q[0]);
  and and_1 (out_1[2], out_1[3], not_1_out);
  and and_2 (out_1[1], not_2_out, register_1_q[0]);
  and and_3 (and_3_out, not_4_out, register_1_q[0]);
  and and_4 (and_4_out, out_1[3], not_5_out);
  Register #(.width(2), .Select("low")) register_1 (
    .D(not_6_out), .Q({out_1[3], register_1_q[0]}), .clk(clock_1_out));  // open: en, clr
  Clock clock_1 (.out(clock_1_out));
  or or_1 (not_6_out[1], and_3_out, and_4_out);
  // Digital_Oscilloscope #(.nState(5)) digital_oscilloscope_1: pin names not known; wires that end beside it: clock_1_out, out_1[3], out_1[2], out_1[1], out_1[0]

  // Notes on the sheet:
  //   W
  //   X
  //   Y
  //   Z
  //   CLK
endmodule

module ex_3_11 (
  output r
);

  wire and_1_out, and_2_out, and_3_out, and_5_out, and_6_out, and_7_out, and_8_out, button_1_out,
       clock_1_out, clock_2_out, not_1_out, not_2_out, not_3_out, not_4_out, not_5_out, not_6_out, not_7_out,
       not_8_out, not_9_out, not_10_out, not_11_out, not_12_out, not_13_out, not_14_out, not_15_out;
  wire [2:0] or_3_out, register_1_q;

  Button button_1 (.out(button_1_out));
  not not_1 (not_1_out, register_1_q[2]);
  not not_2 (not_2_out, register_1_q[1]);
  not not_3 (not_3_out, register_1_q[2]);
  not not_4 (not_4_out, register_1_q[0]);
  not not_5 (not_5_out, register_1_q[1]);
  not not_6 (not_6_out, register_1_q[0]);
  not not_7 (not_7_out, register_1_q[2]);
  not not_8 (not_8_out, register_1_q[2]);
  not not_9 (not_9_out, register_1_q[1]);
  not not_10 (not_10_out, register_1_q[2]);
  not not_11 (not_11_out, register_1_q[0]);
  not not_12 (not_12_out, register_1_q[2]);
  not not_13 (not_13_out, register_1_q[0]);
  not not_14 (not_14_out, register_1_q[2]);
  not not_15 (not_15_out, register_1_q[0]);
  Register #(.width(3), .Select("low")) register_1 (
    .D(or_3_out), .Q(register_1_q), .clk(clock_1_out));  // open: en, clr
  Clock clock_1 (.out(clock_1_out));
  and and_1 (and_1_out, not_1_out, not_2_out, register_1_q[0]);
  and and_2 (and_2_out, not_3_out, register_1_q[1], not_4_out);
  and and_3 (and_3_out, register_1_q[2], not_5_out, not_6_out);
  and and_4 (or_3_out[2], not_7_out, register_1_q[1], register_1_q[0]);
  and and_5 (and_5_out, not_8_out, not_9_out, register_1_q[0]);
  and and_6 (and_6_out, not_10_out, register_1_q[1], not_11_out);
  and and_7 (and_7_out, not_12_out, not_13_out, button_1_out);
  and and_8 (and_8_out, not_14_out, register_1_q[1], not_15_out);
  or or_1 (r, and_1_out, and_2_out, and_3_out);
  or or_2 (or_3_out[1], and_5_out, and_6_out);
  or or_3 (or_3_out[0], and_7_out, and_8_out);
  Clock clock_2 (.out(clock_2_out));
  // Digital_Oscilloscope #(.nState(8)) digital_oscilloscope_1: pin names not known; wires that end beside it: clock_2_out, button_1_out, r
endmodule

module ex_3_13 (
  input  S1,
  input  S0,
  input  X,
  output N1,
  output N0,
  output Y,
  output Z
);

  wire and_1_out, xor_1_out;

  xor xor_1 (xor_1_out, S1, S0);
  and and_1 (and_1_out, ~S1, ~S0);  // AND_Gate
  not not_1 (Y, S1);
  and and_2 (Z, S1, ~S0);  // AND_Gate
  and and_3 (N1, xor_1_out, X);
  and and_4 (N0, and_1_out, X);
endmodule
