// Logisim project ex 3.9 sincronizados de aperto de botao.circ as structural Verilog: 1 circuit, main circuit main
module main (
  output bo
);

  wire and_1_out, and_2_out, button_1_out, clock_1_out, not_1_out, not_2_out, not_3_out, not_4_out, not_5_out;
  wire [1:0] and_3_out, register_1_q;

  Button button_1 (.out(button_1_out));
  not not_1 (not_1_out, register_1_q[1]);
  not not_2 (not_2_out, register_1_q[0]);
  not not_3 (not_3_out, register_1_q[1]);
  not not_4 (not_4_out, register_1_q[0]);
  not not_5 (not_5_out, register_1_q[1]);
  Clock clock_1 (.out(clock_1_out));
  and and_1 (and_1_out, not_1_out, register_1_q[0], button_1_out);
  and and_2 (and_2_out, register_1_q[1], not_2_out, button_1_out);
  and and_3 (and_3_out[0], not_3_out, not_4_out, button_1_out);
  and and_4 (bo, not_5_out, register_1_q[0]);
  Register #(.width(2), .Select("low")) register_1 (
    .D(and_3_out), .Q(register_1_q), .clk(clock_1_out));  // open: en, clr
  or or_1 (and_3_out[1], and_1_out, and_2_out);
  // Digital_Oscilloscope #(.nState(7)) digital_oscilloscope_1: pin names not known; wires that end beside it: clock_1_out, button_1_out, bo
endmodule
