// Logisim project ex fig 2.59.circ as structural Verilog: 6 circuits, main circuit main
module main (
  input  [1:0] in_1,
  input  [1:0] in_2,
  input  [1:0] in_3,
  input  [1:0] in_4,
  output [1:0] out_5
);

  wire button_1_out, clock_1_out, n1_cycle_button_1_bout;
  wire [1:0] controle_1_y;

  Clock clock_1 (.out(clock_1_out));
  Button button_1 (.out(button_1_out));
  _1_Cycle_Button u_1_cycle_button_1 (.B(button_1_out), .Clk(clock_1_out), .Bout(n1_cycle_button_1_bout));
  Multiplexer #(.select(2), .width(2), .enable("false")) multiplexer_1 (
    .in0(in_1), .in1(in_2), .in2(in_3), .in3(in_4), .out(out_5), .sel(controle_1_y));
  Controle controle_1 (.B(clock_1_out), .CLK(n1_cycle_button_1_bout), .X(controle_1_y[1]), .Y(controle_1_y[0]));
endmodule

module Controle (
  input  B,
  input  CLK,
  output X,
  output Y
);

  wire and_1_out, and_2_out, and_3_out, and_4_out, and_5_out, not_1_out, not_2_out, not_3_out, not_4_out,
       not_5_out;
  wire [1:0] or_2_out;

  not not_1 (not_1_out, X);
  and and_1 (and_1_out, not_1_out, Y, B);
  and and_2 (and_2_out, X, not_2_out);
  not not_2 (not_2_out, Y);
  and and_3 (and_3_out, X, not_3_out);
  not not_3 (not_3_out, B);
  not not_4 (not_4_out, Y);
  and and_4 (and_4_out, not_4_out, B);
  and and_5 (and_5_out, Y, not_5_out);
  not not_5 (not_5_out, B);
  Register #(.width(2), .Select("low")) register_1 (.D(or_2_out), .Q({X, Y}), .clk(CLK));  // open: en, clr
  or or_1 (or_2_out[1], and_1_out, and_2_out, and_3_out);
  or or_2 (or_2_out[0], and_4_out, and_5_out);
endmodule

module push_Button (
  input  Bin,
  output Bout
);

  wire and_1_out, clock_1_out, not_1_out;

  Clock clock_1 (.out(clock_1_out));
  not not_1 (not_1_out, Bout);
  and and_1 (and_1_out, not_1_out, Bin);
  Register #(.width(1), .Select("low")) register_1 (.D(and_1_out), .Q(Bout), .clk(clock_1_out));  // open: en, clr
endmodule

module _1_Cycle_Button (
  input  B,
  input  Clk,
  output Bout
);

  wire and_1_out, not_1_out, not_2_out;
  wire [1:0] and_2_out;
  wire [1:1] register_1_q;

  and and_1 (and_1_out, register_1_q[1], B);
  not not_1 (not_1_out, register_1_q[1]);
  not not_2 (not_2_out, Bout);
  Register #(.width(2), .Select("low")) register_1 (
    .D(and_2_out), .Q({register_1_q[1], Bout}), .clk(Clk));  // open: en, clr
  or or_1 (and_2_out[1], Bout, and_1_out);
  and and_2 (and_2_out[0], not_1_out, not_2_out, B);
endmodule

module _2_Bit_Register (
  input  Clk,
  input  d0,
  input  d1,
  output q0,
  output q1
);

  D_Flip_Flop d_ff_1 (.clk(Clk), .D(d0), .Q(q0));  // open: Qn, preset, reset
  D_Flip_Flop d_ff_2 (.clk(Clk), .D(d1), .Q(q1));  // open: Qn, preset, reset
endmodule

module _1_cycle_button_primitive (
  input  B,
  output Bout
);

  wire and_1_out, and_2_out, clock_1_out, n2_bit_register_1_q0, not_1_out, not_2_out, or_1_out;

  and and_1 (and_1_out, n2_bit_register_1_q0, B);
  not not_1 (not_1_out, n2_bit_register_1_q0);
  not not_2 (not_2_out, Bout);
  Clock clock_1 (.out(clock_1_out));
  or or_1 (or_1_out, Bout, and_1_out);
  and and_2 (and_2_out, not_1_out, not_2_out, B);
  _2_Bit_Register u_2_bit_register_1 (
    .d0(or_1_out), .d1(and_2_out), .q0(n2_bit_register_1_q0), .q1(Bout), .Clk(clock_1_out));
endmodule
