// Logisim project maquina refrigerante W.circ as structural Verilog: 4 circuits, main circuit botao
module botao (
  input  bi,
  input  Clk,
  output bo
);

  wire and_1_out, and_2_out, not_1_out, not_2_out, not_3_out, not_4_out, not_5_out;
  wire [1:0] and_3_out, register_1_q;

  not not_1 (not_1_out, register_1_q[1]);
  not not_2 (not_2_out, register_1_q[0]);
  not not_3 (not_3_out, register_1_q[1]);
  not not_4 (not_4_out, register_1_q[0]);
  not not_5 (not_5_out, register_1_q[1]);
  and and_1 (and_1_out, not_1_out, register_1_q[0], bi);
  and and_2 (and_2_out, register_1_q[1], not_2_out, bi);
  and and_3 (and_3_out[0], not_3_out, not_4_out, bi);
  and and_4 (bo, not_5_out, register_1_q[0]);
  Register #(.width(2), .Select("low")) register_1 (.D(and_3_out), .Q(register_1_q), .clk(Clk));  // open: en, clr
  or or_1 (and_3_out[1], and_1_out, and_2_out);
endmodule

module controle (
  input  c,
  input  c_tot_lt_s,
  input  clk,
  output d,
  output tot_clr,
  output tot_ld
);

  wire and_4_out, and_5_out, and_6_out, not_1_out, not_2_out, not_3_out, not_4_out, not_5_out, not_6_out,
       not_7_out, not_8_out, not_9_out;
  wire [1:0] or_2_out, register_1_q;

  and and_1 (d, register_1_q[1], register_1_q[0]);
  not not_1 (not_1_out, register_1_q[1]);
  not not_2 (not_2_out, register_1_q[0]);
  not not_3 (not_3_out, register_1_q[0]);
  not not_4 (not_4_out, register_1_q[1]);
  not not_5 (not_5_out, c_tot_lt_s);
  not not_6 (not_6_out, register_1_q[1]);
  not not_7 (not_7_out, register_1_q[1]);
  not not_8 (not_8_out, c);
  and and_2 (tot_clr, not_1_out, not_2_out);
  and and_3 (tot_ld, register_1_q[1], not_3_out);
  and and_4 (and_4_out, not_4_out, register_1_q[0], not_5_out);
  or or_1 (or_2_out[1], and_4_out, and_5_out);
  and and_5 (and_5_out, not_6_out, register_1_q[0], c);
  and and_6 (and_6_out, not_7_out, not_8_out);
  or or_2 (or_2_out[0], and_6_out, not_9_out);
  not not_9 (not_9_out, register_1_q[0]);
  Register #(.width(2), .Select("low")) register_1 (.D(or_2_out), .Q(register_1_q), .clk(clk));  // open: en, clr
endmodule

module main2 (
  input  [7:0] in_1,
  input  [7:0] in_2,
  output out_3
);

  wire button_1_out, clock_1_out, controle_1_tot_clr, controle_1_tot_ld, main_1_bo, operacional_1_tot_ld_s;

  Button button_1 (.out(button_1_out));
  Clock clock_1 (.out(clock_1_out));
  _1_clockCycle_button_main main_1 (.bi(button_1_out), .Clk(clock_1_out), .bo(main_1_bo));
  controle controle_1 (
    .c(main_1_bo), .c_tot_lt_s(operacional_1_tot_ld_s), .d(out_3), .tot_clr(controle_1_tot_clr),
    .tot_ld(controle_1_tot_ld), .clk(clock_1_out));
  operacional operacional_1 (
    .clr(controle_1_tot_clr), .ld(controle_1_tot_ld), .clk(clock_1_out), .S(in_1),
    .tot_ld_s(operacional_1_tot_ld_s), .A(in_2));
endmodule

module operacional (
  input  clr,
  input  ld,
  input  clk,
  input  [7:0] S,
  input  [7:0] A,
  output tot_ld_s
);

  wire [7:0] adder_1_out, tot_q;

  Comparator #(.mode("unsigned")) comparator_1 (.a(tot_q), .b(S), .lt(tot_ld_s));  // open: gt, eq
  Register #(.Select("low")) tot (.D(adder_1_out), .en(ld), .Q(tot_q), .clk(clk), .clr(clr));
  Adder adder_1 (.a(tot_q), .b(A), .out(adder_1_out));  // open: cin, cout
endmodule
