// Logisim project medidor de distancia a laser.circ as structural Verilog: 3 circuits, main circuit main
module main (
  input  in_1,
  input  in_2,
  output out_3,
  output [15:0] out_4
);

  wire clock_1_out, controle_laser_1_dctr_clr, controle_laser_1_dctr_cnt, controle_laser_1_dreg_clr,
       controle_laser_1_dreg_ld;

  Clock clock_1 (.out(clock_1_out));
  controle_Laser controle_laser_1 (
    .B(in_1), .S(in_2), .L(out_3), .Dreg_clr(controle_laser_1_dreg_clr), .Dreg_ld(controle_laser_1_dreg_ld),
    .Dctr_clr(controle_laser_1_dctr_clr), .Dctr_cnt(controle_laser_1_dctr_cnt), .clk(clock_1_out));
  bloco_operacional bloco_operacional_1 (
    .loadReg(controle_laser_1_dreg_ld), .count(controle_laser_1_dctr_cnt), .clear(controle_laser_1_dctr_clr),
    .clearReg(controle_laser_1_dreg_clr), .clk(clock_1_out), .D(out_4));

  // Notes on the sheet:
  //   distancia (x 10^8 m)
endmodule

module controle_Laser (
  input  B,
  input  S,
  input  clk,
  output L,
  output Dreg_clr,
  output Dreg_ld,
  output Dctr_clr,
  output Dctr_cnt
);

  wire and_6_out, and_7_out, and_8_out, and_9_out, and_10_out, not_1_out, not_2_out, not_3_out, not_4_out,
       not_5_out, not_6_out, not_7_out, not_8_out, not_9_out, not_10_out, not_11_out, not_12_out;
  wire [1:0] register_1_q;
  wire [2:0] or_2_out;

  not not_1 (not_1_out, register_1_q[0]);
  not not_2 (not_2_out, Dreg_ld);
  not not_3 (not_3_out, register_1_q[1]);
  not not_4 (not_4_out, register_1_q[0]);
  not not_5 (not_5_out, register_1_q[1]);
  and and_1 (Dctr_cnt, register_1_q[1], register_1_q[0]);
  and and_2 (or_2_out[2], register_1_q[1], register_1_q[0], S);
  not not_6 (not_6_out, register_1_q[1]);
  not not_7 (not_7_out, register_1_q[0]);
  not not_8 (not_8_out, S);
  not not_9 (not_9_out, register_1_q[1]);
  not not_10 (not_10_out, B);
  not not_11 (not_11_out, S);
  Register #(.width(3), .Select("low")) register_1 (
    .D(or_2_out), .Q({Dreg_ld, register_1_q}), .clk(clk));  // open: en, clr
  and and_3 (L, register_1_q[1], not_1_out);
  and and_4 (Dreg_clr, not_2_out, not_3_out, not_4_out);
  and and_5 (Dctr_clr, not_5_out, register_1_q[0]);
  and and_6 (and_6_out, not_6_out, register_1_q[0], B);
  and and_7 (and_7_out, register_1_q[1], not_7_out);
  and and_8 (and_8_out, register_1_q[1], not_8_out);
  and and_9 (and_9_out, not_9_out, not_10_out);
  not not_12 (not_12_out, register_1_q[0]);
  and and_10 (and_10_out, register_1_q[1], not_11_out);
  or or_1 (or_2_out[1], and_6_out, and_7_out, and_8_out);
  or or_2 (or_2_out[0], and_9_out, not_12_out, and_10_out);

  // Notes on the sheet:
  //   s0
  //   s1
  //   s2
  //   n0
  //   n1
  //   n2
endmodule

module bloco_operacional (
  input  loadReg,
  input  count,
  input  clearReg,
  input  clear,
  input  clk,
  output [15:0] D
);

  wire not_1_out, shift_register_1_out;
  wire [15:0] counter_1_q, shift_register_2_q15;

  Counter #(.width(16), .max('hffff)) counter_1 (
    .count(count), .Q(counter_1_q), .clk(clk), .clr(clear));  // open: load, D, carry, preset, down
  Shift_Register #(.length(2)) shift_register_1 (
    .in(clear), .clk(clk), .out(shift_register_1_out), .clr(count));  // open: shift, load, d0, q0, d1, q1
  Shift_Register #(.length(16)) shift_register_2 (
    .in(1'b0), .clk(clk), .load(loadReg), .d0(counter_1_q[15]), .q0(shift_register_2_q15[15]),
    .d1(counter_1_q[14]), .q1(shift_register_2_q15[14]), .d2(counter_1_q[13]), .q2(shift_register_2_q15[13]),
    .d3(counter_1_q[12]), .q3(shift_register_2_q15[12]), .d4(counter_1_q[11]), .q4(shift_register_2_q15[11]),
    .d5(counter_1_q[10]), .q5(shift_register_2_q15[10]), .d6(counter_1_q[9]), .q6(shift_register_2_q15[9]),
    .d7(counter_1_q[8]), .q7(shift_register_2_q15[8]), .d8(counter_1_q[7]), .q8(shift_register_2_q15[7]),
    .d9(counter_1_q[6]), .q9(shift_register_2_q15[6]), .d10(counter_1_q[5]), .q10(shift_register_2_q15[5]),
    .d11(counter_1_q[4]), .q11(shift_register_2_q15[4]), .d12(counter_1_q[3]), .q12(shift_register_2_q15[3]),
    .d13(counter_1_q[2]), .q13(shift_register_2_q15[2]), .d14(counter_1_q[1]), .q14(shift_register_2_q15[1]),
    .d15(counter_1_q[0]), .q15(shift_register_2_q15[0]));  // open: shift, out, clr
  not not_1 (not_1_out, shift_register_1_out);
  Register #(.width(16), .Select("low")) register_1 (
    .D(shift_register_2_q15), .en(not_1_out), .Q(D), .clk(clk), .clr(clearReg));
endmodule
