// Logisim project registrador ex 4-7.circ as structural Verilog: 4 circuits, main circuit main
module main (
  input  I3,
  input  I2,
  input  I1,
  input  I0,
  input  clr,
  input  set,
  input  ld,
  input  shl,
  output [3:0] out_9
);

  wire clock_1_out, multiplexer_1_out, multiplexer_2_out, multiplexer_3_out, multiplexer_4_out;
  wire [2:0] select;

  Clock clock_1 (.out(clock_1_out));
  s2 s2_1 (.clr(clr), .set(set), .s2(select[2]));
  s1 s1_1 (.clr(clr), .set(set), .ld(ld), .shl(shl), .s1(select[1]));
  s0 s0_1 (.clr(clr), .set(set), .ld(ld), .s0(select[0]));
  Multiplexer #(.select(3), .enable("false")) multiplexer_1 (
    .in0(out_9[3]), .in1(I3), .in2(out_9[2]), .in3(1'b0), .in4(1'b1), .out(multiplexer_1_out), .sel(select));  // open: in5, in6, in7
  D_Flip_Flop d_ff_1 (.clk(clock_1_out), .D(multiplexer_1_out), .Q(out_9[3]));  // open: Qn, preset, reset
  Multiplexer #(.select(3), .enable("false")) multiplexer_2 (
    .in0(out_9[2]), .in1(I2), .in2(out_9[1]), .in3(1'b0), .in4(1'b1), .out(multiplexer_2_out), .sel(select));  // open: in5, in6, in7
  D_Flip_Flop d_ff_2 (.clk(clock_1_out), .D(multiplexer_2_out), .Q(out_9[2]));  // open: Qn, preset, reset
  Multiplexer #(.select(3), .enable("false")) multiplexer_3 (
    .in0(out_9[1]), .in1(I1), .in2(out_9[0]), .in3(1'b0), .in4(1'b1), .out(multiplexer_3_out), .sel(select));  // open: in5, in6, in7
  D_Flip_Flop d_ff_3 (.clk(clock_1_out), .D(multiplexer_3_out), .Q(out_9[1]));  // open: Qn, preset, reset
  Multiplexer #(.select(3), .enable("false")) multiplexer_4 (
    .in0(out_9[0]), .in1(I0), .in2(1'b0), .in3(1'b0), .in4(1'b1), .out(multiplexer_4_out), .sel(select));  // open: in5, in6, in7
  D_Flip_Flop d_ff_4 (.clk(clock_1_out), .D(multiplexer_4_out), .Q(out_9[0]));  // open: Qn, preset, reset

  // Notes on the sheet:
  //   Circuito de seleção
endmodule

module s2 (
  input  clr,
  input  set,
  output s2
);

  wire not_1_out;

  not not_1 (not_1_out, clr);
  and and_1 (s2, not_1_out, set);
endmodule

module s1 (
  input  clr,
  input  set,
  input  ld,
  input  shl,
  output s1
);

  wire and_1_out, not_1_out, not_2_out, not_3_out;

  not not_1 (not_1_out, clr);
  not not_2 (not_2_out, set);
  not not_3 (not_3_out, ld);
  and and_1 (and_1_out, not_1_out, not_2_out, not_3_out, shl);
  or or_1 (s1, and_1_out, clr);
endmodule

module s0 (
  input  clr,
  input  set,
  input  ld,
  output s0
);

  wire and_1_out, not_1_out, not_2_out;

  not not_1 (not_1_out, clr);
  not not_2 (not_2_out, set);
  and and_1 (and_1_out, not_1_out, not_2_out, ld);
  or or_1 (s0, and_1_out, clr);
endmodule
