// Logisim project seletor de operacoes.circ as structural Verilog: 2 circuits, main circuit main
module main (
  input  [7:0] in_1,
  input  [7:0] in_2,
  input  [1:0] \Opção ,
  output [7:0] Resultado
);

  wire [7:0] adder_1_out, divider_1_out, multiplier_1_out, subtractor_1_out;

  Adder adder_1 (.a(in_1), .b(in_2), .out(adder_1_out));  // open: cin, cout
  Subtractor subtractor_1 (.a(in_1), .b(in_2), .out(subtractor_1_out));  // open: bin, bout
  Multiplier multiplier_1 (.a(in_1), .b(in_2), .out(multiplier_1_out));  // open: cin, cout
  Divider divider_1 (.a(in_1), .b(in_2), .out(divider_1_out));  // open: upper, rem
  Multiplexer #(.select(2), .width(8), .enable("false")) multiplexer_1 (
    .in0(adder_1_out), .in1(subtractor_1_out), .in2(multiplier_1_out), .in3(divider_1_out), .out(Resultado),
    .sel(\Opção ));

  // Other names for the same wires on the sheet: A[7:0] = in_1; B[7:0] = in_2

  // Notes on the sheet:
  //   Soma
  //   Subtração
  //   Multiplicação
  //   Divisão
  //   0=soma
  //   3=divisão
  //   1=subtração
  //   2=multiplicação
endmodule

module Seletor (
  input  A,
  input  B,
  output a_2,
  output s,
  output m,
  output d
);

  wire not_1_out, not_2_out, not_3_out, not_4_out;

  not not_1 (not_1_out, A);
  not not_2 (not_2_out, B);
  not not_3 (not_3_out, A);
  not not_4 (not_4_out, B);
  and and_1 (d, A, B);
  and and_2 (a_2, not_1_out, not_2_out);
  and and_3 (s, not_3_out, B);
  and and_4 (m, A, not_4_out);
endmodule
