// Logisim project somador 2 bits registrador.circ as structural Verilog: 2 circuits, main circuit main
module main (
  input  b0,
  input  b1,
  input  a1,
  input  a0,
  input  in_5,
  output [1:0] out_6,
  output out_7,
  output out_8
);

  wire and_1_out, and_2_out, and_3_out, and_4_out, and_5_out, and_6_out, clock_1_out, or_2_out;
  wire [1:0] undriven;

  and and_1 (and_1_out, a0, in_5);
  and and_2 (and_2_out, in_5, or_2_out);
  and and_3 (and_3_out, a0, or_2_out);
  // OR_Gate or_1 has open pins: in0=and_1_out, in1=and_3_out, in2=and_2_out, out=open
  ExactlyOne xor_1 (.out(out_7), .in0(a0), .in1(in_5), .in2(or_2_out));
  and and_4 (and_4_out, b1, a1);
  and and_5 (and_5_out, b1, b0);
  and and_6 (and_6_out, a1, b0);
  or or_2 (or_2_out, and_4_out, and_5_out, and_6_out);
  ExactlyOne xor_2 (.out(out_8), .in0(b1), .in1(a1), .in2(b0));
  Clock clock_1 (.out(clock_1_out));
  Register #(.width(2), .Select("low")) register_1 (.D(undriven), .Q(out_6), .clk(clock_1_out));  // open: en, clr
endmodule

module somador_reg (
  input  b1,
  input  b0,
  input  Cin,
  output [1:0] out_4,
  output out_5,
  output out_6
);

  wire and_1_out, and_2_out, and_3_out, and_4_out, and_5_out, and_6_out, clock_1_out, or_2_out;

  and and_1 (and_1_out, b1, or_2_out);
  and and_2 (and_2_out, b1, out_4[1]);
  // OR_Gate or_1 has open pins: in0=and_2_out, in1=and_1_out, in2=and_3_out, out=open
  and and_3 (and_3_out, out_4[1], or_2_out);
  ExactlyOne xor_1 (.out(out_5), .in0(b1), .in1(out_4[1]), .in2(or_2_out));
  and and_4 (and_4_out, out_4[0], Cin);
  and and_5 (and_5_out, out_4[0], b0);
  or or_2 (or_2_out, and_5_out, and_4_out, and_6_out);
  and and_6 (and_6_out, b0, Cin);
  ExactlyOne xor_2 (.out(out_6), .in0(out_4[0]), .in1(b0), .in2(Cin));
  Register #(.width(2), .Select("low")) register_1 (.D({out_5, out_6}), .Q(out_4), .clk(clock_1_out));  // open: en, clr
  Clock clock_1 (.out(clock_1_out));
endmodule
